// Logisim project cpu.circ as structural Verilog: 12 circuits, main circuit ◇单周期MIPS(硬布线)
module \单周期MIPS_硬布线  (
  output RegWrite,
  output MemWrite,
  output [31:0] PC,
  output [31:0] IR,
  output [31:0] RDin,
  output [31:0] MDin
);

  wire CLK, clock_1_out, clock_2_out, comparator_1_eq, comparator_1_lt, d_ff_1_q, nand_1_out, RST;
  wire [9:0] PC_q;
  wire [12:0] CNT_num;
  wire [15:0] \总周期数 ;
  wire [31:0] mips_probe_1_p3;

  Button \u_总复位  (.out(RST));
  Clock #(.highDuration(1), .lowDuration(1)) clock_1 (.out(clock_1_out));
  Register #(.width(10), .trigger("rising"), .Select("low")) u_PC (.Q(PC_q));  // open: D, en, clk, clr
  D_Flip_Flop #(.trigger("high"), .Pre_Clr_Positions("LEGACY"), .NegatePresetClear("false"), .enable("true"), .NewFFLayout("false")) d_ff_1 (.Q(d_ff_1_q));  // open: clk, D, Qn, preset, en, reset
  // Probe on 13'hc
  // Probe on \总周期数 
  // Probe on \总周期数 
  // Mips_Probe mips_probe_1: pin names not known; wires that end beside it: clock_1_out, CLK, mips_probe_1_p3
  RAM #(.addrWidth(10), .dataWidth(32), .bus("separate"), .Select("high")) ram_1 (
    .addr(PC_q), .data(mips_probe_1_p3));  // open: din, str, sel, clk, ld, clr
  Comparator #(.width(13), .mode("twosComplement")) comparator_1 (
    .a(CNT_num), .b(13'hc), .eq(comparator_1_eq), .lt(comparator_1_lt));  // open: gt
  Clock #(.highDuration(1), .lowDuration(1)) clock_2 (.out(clock_2_out));
  nand nand_1 (nand_1_out, d_ff_1_q, comparator_1_eq);
  Counter #(.width(13), .max('h1fff), .ongoal("stay"), .trigger("rising"), .behavior("old")) counter_1 (
    .count(comparator_1_lt), .Q(CNT_num), .clk(clock_2_out));  // open: load, D, carry, clr, preset
  assign CLK = nand_1_out ? clock_2_out : 1'bz;  // Controlled_Buffer controlled_buffer_1
  Pull_Resistor #(.pull(1)) pull_resistor_1 (.node(CLK));
  MIPS_Regifile mips_regifile_1 ();  // open: Din, Clk, R1, R2, WE, W_num, R1_num, R2_num
  MIPS_ALU mips_alu_1 ();  // open: X, Y, AluOP, Equal, Result, Result_2
  \单周期硬布线控制器  \u_单周期硬布线控制器_1  ();  // open: Func, RegWrite, MemToReg, MemWrite, Beq, Bne, RegDst, AluSrc, ALU_OP, OP, Halt

  // Notes on the sheet:
  //   程序运行结束后可停机，查看数据存储器中80单元的排序情况是有符号降序
  //   控制位
  //   暂停节拍，不能为0
  //   总周期数参考值：224
  //   用这个时钟源需要去掉电路中的其他时钟源
  //   MIPS反汇编探针
  //   戳工具置1进入计数暂停模式，ctrl+k时钟自动运行到对应节拍暂停
  //   ctrl+k关闭时钟连续运行，将控制位置零，进入单步调试模式调试
  //   可计数暂停的时钟源
  //   为方便自动评测，需要输出PC，IR，寄存器文件写入端口RDin，内存写入端口MDin等信号，以上引脚不能悬空
endmodule

// 单周期硬布线控制器
module \单周期硬布线控制器  (
  input  [5:0] OP,
  input  [5:0] Func,
  output [3:0] ALU_OP,
  output RegDst,
  output RegWrite,
  output MemToReg,
  output MemWrite,
  output AluSrc,
  output Beq,
  output Bne,
  output Halt
);

  wire ADDI, BEQ_t, BNE_t, comparator_6_eq, LW, SW;
  wire [5:0] undriven, undriven_2, undriven_3, undriven_4, undriven_5;

  Comparator #(.width(6), .mode("twosComplement")) comparator_1 (.a(OP), .b(undriven), .eq(LW));  // open: gt, lt
  Comparator #(.width(6), .mode("twosComplement")) comparator_2 (.a(OP), .b(undriven_2), .eq(SW));  // open: gt, lt
  Comparator #(.width(6), .mode("twosComplement")) comparator_3 (.a(OP), .b(undriven_3), .eq(BEQ_t));  // open: gt, lt
  Comparator #(.width(6), .mode("twosComplement")) comparator_4 (.a(OP), .b(undriven_4), .eq(BNE_t));  // open: gt, lt
  Comparator #(.width(6), .mode("twosComplement")) comparator_5 (.a(OP), .b(undriven_5), .eq(ADDI));  // open: gt, lt
  Comparator #(.width(6), .mode("twosComplement")) comparator_6 (
    .a(OP), .b({6{1'b0}}), .eq(comparator_6_eq));  // open: gt, lt

  // Notes on the sheet:
  //   指令译码信号
  //   指令译码逻辑
  //   给出简单的逻辑实现对应指令译码信号，LW、SW、BEQ、BNE、ADDI、ADD、SLT、SYSCALL、R_TYPE。
  //   ALU控制器逻辑
  //   注意R_TYPE表示R型运算指令，SYSCALL是特殊的R型指令，不属于这个类别
  //   根据指令译码信号实现控制器输出控制信号的逻辑
  //   给出简单的逻辑实现ALU_OP与OP、Func之间的对应关系
  //   控制信号
endmodule

module \多周期MIPS_微程序  (
  output RegWrite,
  output MemWrite,
  output [31:0] PC,
  output [31:0] IR,
  output [31:0] RDin,
  output [31:0] MDin
);

  wire ALUSRCA, and_1_out, and_2_out, BEQ, BNE, CLK, clock_2_out, comparator_1_eq, comparator_1_lt,
       comparator_2_eq, controlled_buffer_1_out, d_ff_1_q, IorD, IRW, mips_alu_1_equal, mips_ram_1_p5,
       MM2REG, MMR, MMW, nand_1_out, not_1_out, not_2_out, or_1_out, PCSRC, PCW, REGDST, REGW, RST,
       \多周期微程序控制器_1_alusrca , \多周期微程序控制器_1_beq , \多周期微程序控制器_1_bne , \多周期微程序控制器_1_iord ,
       \多周期微程序控制器_1_irwrite , \多周期微程序控制器_1_memtoreg , \多周期微程序控制器_1_pcsrc , \多周期微程序控制器_1_pcwrite ,
       \多周期微程序控制器_1_regdst ;
  wire [1:0] ALUSRCB, multiplexer_1_out, \多周期微程序控制器_1_alusrcb ;
  wire [3:0] ALUOP, mips_probe_1_p3, STATE_WORD, \多周期微程序控制器_1_alu_op , \微地址 ;
  wire [4:0] multiplexer_4_out;
  wire [5:0] FUNC, OP;
  wire [12:0] CNT_num;
  wire [13:0] multiplexer_1_out_3;
  wire [15:0] multiplexer_1_out_2, multiplexer_2_out, \总周期数 ;
  wire [31:0] C_q, DR_q, mips_alu_1_result, mips_probe_2_p1, multiplexer_5_out, multiplexer_6_out,
       multiplexer_7_out, registerfile_1_p5, registerfile_1_p6, registerfile_1_p7, shifter_1_out;

  Button \u_总复位  (.out(RST));
  Clock #(.highDuration(1), .lowDuration(1)) clock_1 (.out(CLK));
  D_Flip_Flop #(.trigger("high"), .Pre_Clr_Positions("LEGACY"), .NegatePresetClear("false"), .enable("true"), .NewFFLayout("false")) d_ff_1 (.Q(d_ff_1_q));  // open: clk, D, Qn, preset, en, reset
  Register #(.width(32), .trigger("rising"), .Select("low")) u_PC (
    .D(multiplexer_7_out), .en(or_1_out), .Q(PC), .clk(CLK), .clr(RST));
  Counter #(.width(16), .max('hffff), .ongoal("wrap"), .trigger("rising"), .behavior("new")) counter_1 (
    .count(not_1_out), .Q(\总周期数 ), .clk(CLK), .clr(RST));  // open: load, D, carry, preset, down
  // Probe on 13'h61
  // Probe on \微地址 
  // Probe on \总周期数 
  // Probe on \总周期数 
  Multiplexer #(.select(1), .width(32), .disabled("Z"), .enable("false")) multiplexer_1 (
    .in0(PC), .in1(C_q), .out({multiplexer_1_out_3, multiplexer_1_out_2, multiplexer_1_out}),
    .sel(\多周期微程序控制器_1_iord ));
  Comparator #(.width(13), .mode("twosComplement")) comparator_1 (
    .a(CNT_num), .b(13'h61), .eq(comparator_1_eq), .lt(comparator_1_lt));  // open: gt
  Clock #(.highDuration(1), .lowDuration(1)) clock_2 (.out(clock_2_out));
  not not_1 (not_1_out, comparator_2_eq);
  Comparator #(.width(32), .mode("twosComplement")) comparator_2 (
    .a(IR), .b(32'hc), .eq(comparator_2_eq));  // open: gt, lt
  Button \u_总复位_2  ();  // open: out
  nand nand_1 (nand_1_out, d_ff_1_q, comparator_1_eq);
  Counter #(.width(13), .max('h1fff), .ongoal("stay"), .trigger("rising"), .behavior("old")) counter_2 (
    .count(comparator_1_lt), .Q(CNT_num), .clk(clock_2_out), .clr(RST));  // open: load, D, carry, preset
  // Probe on mips_probe_1_p3
  // Mips_Probe mips_probe_1: pin names not known; wires that end beside it: IR, \微地址 , mips_probe_1_p3
  // Mips_Probe mips_probe_2: pin names not known; wires that end beside it: mips_probe_2_p1
  // MIPS_RAM mips_ram_1: pin names not known; wires that end beside it: multiplexer_1_out_2, MDin, CNT_num, CLK, mips_ram_1_p5, mips_probe_2_p1
  assign controlled_buffer_1_out = nand_1_out ? clock_2_out : 1'bz;  // Controlled_Buffer controlled_buffer_1
  Pull_Resistor #(.pull(1)) pull_resistor_1 (.node(controlled_buffer_1_out));
  Register #(.width(32), .trigger("rising"), .Select("low")) u_IR (
    .D(mips_probe_2_p1), .en(\多周期微程序控制器_1_irwrite ), .Q(IR), .clk(CLK), .clr(RST));
  \多周期微程序控制器  \u_多周期微程序控制器_1  (
    .PcWrite(\多周期微程序控制器_1_pcwrite ), .Beq(\多周期微程序控制器_1_beq ), .PCsrc(\多周期微程序控制器_1_pcsrc ),
    .AluSrcB(\多周期微程序控制器_1_alusrcb ), .AluSrcA(\多周期微程序控制器_1_alusrca ), .RegWrite(RegWrite),
    .MemToReg(\多周期微程序控制器_1_memtoreg ), .RegDst(\多周期微程序控制器_1_regdst ), .IorD(\多周期微程序控制器_1_iord ),
    .MemWrite(MemWrite), .MemRead(mips_ram_1_p5), .IrWrite(\多周期微程序控制器_1_irwrite ), .Bne(\多周期微程序控制器_1_bne ),
    .CLK(CLK), .\当前微指令地址 (mips_probe_1_p3), .RST(RST), .OP(IR[31:26]), .ALU_OP(\多周期微程序控制器_1_alu_op ),
    .Func(IR[5:0]));
  Register #(.width(32), .trigger("rising"), .Select("low")) DR (
    .D(mips_probe_2_p1), .Q(DR_q), .clk(CLK), .clr(RST));  // open: en
  Multiplexer #(.select(1), .width(16), .disabled("Z"), .enable("false")) multiplexer_2 (
    .in0({16{1'b0}}), .in1({16{1'b1}}), .out(multiplexer_2_out), .sel(IR[15]));
  Multiplexer #(.select(1), .width(32), .disabled("Z"), .enable("false")) multiplexer_3 (
    .in0(C_q), .in1(DR_q), .out(RDin), .sel(\多周期微程序控制器_1_memtoreg ));
  Multiplexer #(.select(1), .width(5), .disabled("Z"), .enable("false")) multiplexer_4 (
    .in0(IR[20:16]), .in1(IR[15:11]), .out(multiplexer_4_out), .sel(\多周期微程序控制器_1_regdst ));
  Shifter #(.width(32), .shift("ll")) shifter_1 (
    .in({multiplexer_2_out, IR[15:0]}), .\dist (5'b00010), .out(shifter_1_out));
  // RegisterFile registerfile_1: pin names not known; wires that end beside it: CLK, multiplexer_4_out, IR[25:21], IR[20:16], registerfile_1_p5, registerfile_1_p6, registerfile_1_p7
  Register #(.width(32), .trigger("rising"), .Select("low")) A (
    .D(registerfile_1_p5), .Q(registerfile_1_p7), .clk(CLK), .clr(RST));  // open: en
  Register #(.width(32), .trigger("rising"), .Select("low")) B (
    .D(registerfile_1_p6), .Q(MDin), .clk(CLK), .clr(RST));  // open: en
  Multiplexer #(.select(1), .width(32), .disabled("Z"), .enable("false")) multiplexer_5 (
    .in0(PC), .in1(registerfile_1_p7), .out(multiplexer_5_out), .sel(\多周期微程序控制器_1_alusrca ));
  Multiplexer #(.select(2), .width(32), .disabled("Z"), .enable("false")) multiplexer_6 (
    .in0(MDin), .in1(32'h4), .in2({multiplexer_2_out, IR[15:0]}), .in3(shifter_1_out),
    .out(multiplexer_6_out), .sel(\多周期微程序控制器_1_alusrcb ));
  // Probe on multiplexer_5_out
  MIPS_ALU mips_alu_1 (
    .X(multiplexer_5_out), .Y(multiplexer_6_out), .AluOP(\多周期微程序控制器_1_alu_op ), .Equal(mips_alu_1_equal),
    .Result(mips_alu_1_result));  // open: Result_2
  // Probe on multiplexer_6_out
  not not_2 (not_2_out, mips_alu_1_equal);
  // Probe on mips_alu_1_result
  \多周期硬布线控制器  \u_多周期硬布线控制器_1  (
    .RST(RST), .AluSrcB(ALUSRCB), .OP(OP), .CLK(CLK), .\当前状态 (STATE_WORD), .IorD(IorD), .PCsrc(PCSRC),
    .AluSrcA(ALUSRCA), .MemToReg(MM2REG), .RegDst(REGDST), .IrWrite(IRW), .PcWrite(PCW), .RegWrite(REGW),
    .MemWrite(MMW), .MemRead(MMR), .Beq(BEQ), .Bne(BNE), .Func(FUNC), .ALU_OP(ALUOP));
  and and_1 (and_1_out, \多周期微程序控制器_1_beq , mips_alu_1_equal);
  and and_2 (and_2_out, \多周期微程序控制器_1_bne , not_2_out);
  Register #(.width(32), .trigger("rising"), .Select("low")) C (
    .D(mips_alu_1_result), .Q(C_q), .clk(CLK), .clr(RST));  // open: en
  or or_1 (or_1_out, \多周期微程序控制器_1_pcwrite , and_1_out, and_2_out);
  // Probe on C_q
  Multiplexer #(.select(1), .width(32), .disabled("Z"), .enable("false")) multiplexer_7 (
    .in0(mips_alu_1_result), .in1(C_q), .out(multiplexer_7_out), .sel(\多周期微程序控制器_1_pcsrc ));

  // Notes on the sheet:
  //   控制位
  //   暂停节拍，不能为0
  //   加载sort.hex，程序执行会停机并进行内存排序
  //   用这个时钟源需要去掉电路中的其他时钟源
  //   戳工具置1进入计数暂停模式，ctrl+k时钟自动运行到对应节拍暂停
  //   ctrl+k关闭时钟连续运行，将控制位置零，进入单步调试模式调试
  //   参考值：891
  //   可计数暂停的时钟源
  //   部件
  //   选择器
  //   部件
  //   选择器
  //   指令译码
endmodule

// 微程序控制器
module \多周期微程序控制器  (
  input  [5:0] OP,
  input  [5:0] Func,
  input  CLK,
  input  RST,
  output [3:0] ALU_OP,
  output Bne,
  output Beq,
  output MemRead,
  output MemWrite,
  output RegWrite,
  output PcWrite,
  output IrWrite,
  output RegDst,
  output MemToReg,
  output [3:0] \当前微指令地址 ,
  output [1:0] AluSrcB,
  output AluSrcA,
  output PCsrc,
  output IorD
);

  wire ADD, ADDI, BEQ_t, BNE_t, comparator_6_eq, LW, P, R_TYPE, SLT, SW, SysCall;
  wire [1:0] ALU_Control;
  wire [3:0] multiplexer_1_out, multiplexer_2_out, multiplexer_3_out, or_1_out, rom_1_data, \微程序地址转移逻辑_1_s0 ;

  Comparator #(.width(6), .mode("twosComplement")) comparator_1 (.a(OP), .b(6'b100011), .eq(LW));  // open: gt, lt
  Comparator #(.width(6), .mode("twosComplement")) comparator_2 (.a(OP), .b(6'b101011), .eq(SW));  // open: gt, lt
  Comparator #(.width(6), .mode("twosComplement")) comparator_3 (.a(OP), .b(6'b000100), .eq(BEQ_t));  // open: gt, lt
  Comparator #(.width(6), .mode("twosComplement")) comparator_4 (.a(OP), .b(6'b000101), .eq(BNE_t));  // open: gt, lt
  Comparator #(.width(6), .mode("twosComplement")) comparator_5 (.a(OP), .b(6'b001000), .eq(ADDI));  // open: gt, lt
  Comparator #(.width(6), .mode("twosComplement")) comparator_6 (
    .a(OP), .b({6{1'b0}}), .eq(comparator_6_eq));  // open: gt, lt
  and and_1 (R_TYPE, ~SysCall, comparator_6_eq);  // AND_Gate
  \微程序地址转移逻辑  \u_微程序地址转移逻辑_1  (
    .R_Type(R_TYPE), .S3(\微程序地址转移逻辑_1_s0 [3]), .ADDI(ADDI), .S2(\微程序地址转移逻辑_1_s0 [2]), .LW(LW),
    .S1(\微程序地址转移逻辑_1_s0 [1]), .SW(SW), .S0(\微程序地址转移逻辑_1_s0 [0]), .BEQ(BEQ_t), .BNE(BNE_t), .SYSCALL(SysCall));
  Comparator #(.width(6), .mode("twosComplement")) comparator_7 (.a(Func), .b(6'b100000), .eq(ADD));  // open: gt, lt
  Comparator #(.width(6), .mode("twosComplement")) comparator_8 (.a(Func), .b(6'b101010), .eq(SLT));  // open: gt, lt
  and and_2 (SysCall, ~SLT, ~ADD, comparator_6_eq);  // AND_Gate
  Register #(.width(4), .trigger("rising"), .Select("low")) register_1 (
    .D(multiplexer_1_out), .Q(\当前微指令地址 ), .clk(CLK), .clr(RST));  // open: en
  Multiplexer #(.select(1), .width(4), .disabled("Z"), .enable("false")) multiplexer_1 (
    .in0(rom_1_data), .in1(\微程序地址转移逻辑_1_s0 ), .out(multiplexer_1_out), .sel(P));
  ROM #(.addrWidth(4), .dataWidth(21), .Select("high")) rom_1 (
    .addr(\当前微指令地址 ),
    .data({IorD, PCsrc, AluSrcA, AluSrcB, MemToReg, RegDst, IrWrite, PcWrite, RegWrite, MemWrite, MemRead, Beq, Bne, ALU_Control, P, rom_1_data}));
  Multiplexer #(.select(1), .width(4), .disabled("Z"), .enable("false")) multiplexer_2 (
    .in0(4'b0000), .in1(4'b0101), .out(multiplexer_2_out), .sel(ADD));
  Multiplexer #(.select(1), .width(4), .disabled("Z"), .enable("false")) multiplexer_3 (
    .in0(4'b0000), .in1(4'b1011), .out(multiplexer_3_out), .sel(SLT));
  assign or_1_out = 4'b0000 | multiplexer_2_out | multiplexer_3_out;  // OR_Gate or_1, 4 bits wide
  Multiplexer #(.select(2), .width(4), .disabled("Z"), .enable("false")) multiplexer_4 (
    .in0(4'b0101), .in1(4'b0110), .in2(or_1_out), .out(ALU_OP), .sel(ALU_Control));  // open: in3

  // Notes on the sheet:
  //   指令译码信号
  //   根据指令进行微程序地址转移
  //   指令译码逻辑
  //   给出简单的逻辑实现对应指令译码信号，LW、SW、BEQ、BNE、ADDI、ADD、SLT、SYSCALL、R_TYPE。
  //   下址字段
  //   微程序
  //   入口地址
  //   判断逻辑
  //   μAR
  //   控制存储器
  //   contents of rom_1 (hex, n*v repeats v):
  //   13201 30010 60003 100204 8800 60006 100400 40048 4800 c0100 c0080 6000c 800 10004d
  //   微命令
  //   ALU控制器逻辑
  //   根据ALU_Control的值决定运算器运算选择控制信号ALU_OP的值
  //   注意R_TYPE表示R型运算指令，SYSCALL是特殊的R型指令，不属于这个类别
  //   微指令
  //   下址字段
  //   判断逻辑
  //   ALU_Control= 00 运算器做加法
  //   ALU_Control= 01 运算器做减法
  //   ALU_Control= 10 运算方式由Func决定 
endmodule

// 地址转移逻辑
module \微程序地址转移逻辑  (
  input  R_Type,
  input  ADDI,
  input  LW,
  input  SW,
  input  BEQ,
  input  BNE,
  input  SYSCALL,
  output S3,
  output S2,
  output S1,
  output S0
);

  wire [3:0] multiplexer_1_out, multiplexer_2_out, multiplexer_3_out, multiplexer_4_out, multiplexer_5_out,
       multiplexer_6_out, multiplexer_7_out;

  Multiplexer #(.select(1), .width(4), .disabled("Z"), .enable("false")) multiplexer_1 (
    .in0(4'b0000), .in1(4'b0111), .out(multiplexer_1_out), .sel(R_Type));
  Multiplexer #(.select(1), .width(4), .disabled("Z"), .enable("false")) multiplexer_2 (
    .in0(4'b0000), .in1(4'b1011), .out(multiplexer_2_out), .sel(ADDI));
  Multiplexer #(.select(1), .width(4), .disabled("Z"), .enable("false")) multiplexer_3 (
    .in0(4'b0000), .in1(4'b0010), .out(multiplexer_3_out), .sel(LW));
  Multiplexer #(.select(1), .width(4), .disabled("Z"), .enable("false")) multiplexer_4 (
    .in0(4'b0000), .in1(4'b0101), .out(multiplexer_4_out), .sel(SW));
  Multiplexer #(.select(1), .width(4), .disabled("Z"), .enable("false")) multiplexer_5 (
    .in0(4'b0000), .in1(4'b1001), .out(multiplexer_5_out), .sel(BEQ));
  Multiplexer #(.select(1), .width(4), .disabled("Z"), .enable("false")) multiplexer_6 (
    .in0(4'b0000), .in1(4'b1010), .out(multiplexer_6_out), .sel(BNE));
  Multiplexer #(.select(1), .width(4), .disabled("Z"), .enable("false")) multiplexer_7 (
    .in0(4'b0000), .in1(4'b1101), .out(multiplexer_7_out), .sel(SYSCALL));
  assign {S3, S2, S1, S0} = multiplexer_1_out | multiplexer_2_out | multiplexer_3_out | multiplexer_4_out | multiplexer_5_out | multiplexer_6_out | multiplexer_7_out;  // OR_Gate or_1, 4 bits wide
endmodule

module \多周期MIPS_硬布线  (
  output RegWrite,
  output MemWrite,
  output [31:0] PC,
  output [31:0] IR,
  output [31:0] RDin,
  output [31:0] MDin
);

  wire ALUSRCA, and_1_out, and_2_out, BEQ, BNE, CLK, clock_2_out, comparator_1_eq, comparator_1_lt,
       comparator_2_eq, d_ff_1_q, IorD, IRW, mips_alu_1_equal, mips_ram_1_p4, MM2REG, MMR, MMW, nand_1_out,
       not_1_out, not_2_out, or_1_out, PCSRC, PCW, REGDST, REGW, RST, \多周期硬布线控制器_1_alusrca ,
       \多周期硬布线控制器_1_beq , \多周期硬布线控制器_1_bne , \多周期硬布线控制器_1_iord , \多周期硬布线控制器_1_irwrite ,
       \多周期硬布线控制器_1_memtoreg , \多周期硬布线控制器_1_pcsrc , \多周期硬布线控制器_1_pcwrite , \多周期硬布线控制器_1_regdst ;
  wire [1:0] ALUSRCB, multiplexer_1_out, \多周期硬布线控制器_1_alusrcb ;
  wire [3:0] ALUOP, mips_probe_1_p3, STATE_WORD, \多周期硬布线控制器_1_alu_op , \微地址 , \现态 ;
  wire [4:0] multiplexer_4_out;
  wire [5:0] FUNC, OP;
  wire [12:0] CNT_num;
  wire [13:0] multiplexer_1_out_3;
  wire [15:0] multiplexer_1_out_2, multiplexer_2_out, \总周期数 ;
  wire [31:0] C_q, DR_q, mips_alu_1_result, mips_probe_2_p1, multiplexer_5_out, multiplexer_6_out,
       multiplexer_7_out, registerfile_1_p5, registerfile_1_p6, registerfile_1_p7, shifter_1_out;

  Button \u_总复位  (.out(RST));
  Clock #(.highDuration(1), .lowDuration(1)) clock_1 ();  // open: out
  D_Flip_Flop #(.trigger("high"), .Pre_Clr_Positions("LEGACY"), .NegatePresetClear("false"), .enable("true"), .NewFFLayout("false")) d_ff_1 (.Q(d_ff_1_q));  // open: clk, D, Qn, preset, en, reset
  // Probe on 13'hc
  // Probe on \现态 
  Comparator #(.width(13), .mode("twosComplement")) comparator_1 (
    .a(CNT_num), .b(13'hc), .eq(comparator_1_eq), .lt(comparator_1_lt));  // open: gt
  Clock #(.highDuration(1), .lowDuration(1)) clock_2 (.out(clock_2_out));
  Register #(.width(32), .trigger("rising"), .Select("low")) u_PC (
    .D(multiplexer_7_out), .en(or_1_out), .Q(PC), .clk(CLK), .clr(RST));
  Counter #(.width(16), .max('hffff), .ongoal("wrap"), .trigger("rising"), .behavior("new")) counter_1 (
    .count(not_1_out), .Q(\总周期数 ), .clk(CLK), .clr(RST));  // open: load, D, carry, preset, down
  // Probe on \总周期数 
  // Probe on \总周期数 
  nand nand_1 (nand_1_out, d_ff_1_q, comparator_1_eq);
  Counter #(.width(13), .max('h1fff), .ongoal("stay"), .trigger("rising"), .behavior("old")) counter_2 (
    .count(comparator_1_lt), .Q(CNT_num), .clk(clock_2_out));  // open: load, D, carry, clr, preset
  Multiplexer #(.select(1), .width(32), .disabled("Z"), .enable("false")) multiplexer_1 (
    .in0(PC), .in1(C_q), .out({multiplexer_1_out_3, multiplexer_1_out_2, multiplexer_1_out}),
    .sel(\多周期硬布线控制器_1_iord ));
  assign CLK = nand_1_out ? clock_2_out : 1'bz;  // Controlled_Buffer controlled_buffer_1
  Pull_Resistor #(.pull(1)) pull_resistor_1 (.node(CLK));
  Comparator #(.width(32), .mode("twosComplement")) comparator_2 (
    .a(IR), .b(32'hc), .eq(comparator_2_eq));  // open: gt, lt
  not not_1 (not_1_out, comparator_2_eq);
  // Probe on mips_probe_1_p3
  // Mips_Probe mips_probe_1: pin names not known; wires that end beside it: IR, \微地址 , mips_probe_1_p3
  // Mips_Probe mips_probe_2: pin names not known; wires that end beside it: mips_probe_2_p1
  // MIPS_RAM mips_ram_1: pin names not known; wires that end beside it: multiplexer_1_out_2, MDin, CLK, mips_ram_1_p4, mips_probe_2_p1
  \多周期硬布线控制器  \u_多周期硬布线控制器_1  (
    .RST(RST), .AluSrcB(\多周期硬布线控制器_1_alusrcb ), .OP(IR[31:26]), .CLK(CLK), .\当前状态 (mips_probe_1_p3),
    .IorD(\多周期硬布线控制器_1_iord ), .PCsrc(\多周期硬布线控制器_1_pcsrc ), .AluSrcA(\多周期硬布线控制器_1_alusrca ),
    .MemToReg(\多周期硬布线控制器_1_memtoreg ), .RegDst(\多周期硬布线控制器_1_regdst ), .IrWrite(\多周期硬布线控制器_1_irwrite ),
    .PcWrite(\多周期硬布线控制器_1_pcwrite ), .RegWrite(RegWrite), .MemWrite(MemWrite), .MemRead(mips_ram_1_p4),
    .Beq(\多周期硬布线控制器_1_beq ), .Bne(\多周期硬布线控制器_1_bne ), .Func(IR[5:0]), .ALU_OP(\多周期硬布线控制器_1_alu_op ));
  Register #(.width(32), .trigger("rising"), .Select("low")) u_IR (
    .D(mips_probe_2_p1), .en(\多周期硬布线控制器_1_irwrite ), .Q(IR), .clk(CLK), .clr(RST));
  Register #(.width(32), .trigger("rising"), .Select("low")) DR (
    .D(mips_probe_2_p1), .Q(DR_q), .clk(CLK), .clr(RST));  // open: en
  Multiplexer #(.select(1), .width(16), .disabled("Z"), .enable("false")) multiplexer_2 (
    .in0({16{1'b0}}), .in1({16{1'b1}}), .out(multiplexer_2_out), .sel(IR[15]));
  Multiplexer #(.select(1), .width(32), .disabled("Z"), .enable("false")) multiplexer_3 (
    .in0(C_q), .in1(DR_q), .out(RDin), .sel(\多周期硬布线控制器_1_memtoreg ));
  \多周期硬布线控制器  \u_多周期硬布线控制器_2  (
    .RST(RST), .AluSrcB(ALUSRCB), .OP(OP), .CLK(CLK), .\当前状态 (STATE_WORD), .IorD(IorD), .PCsrc(PCSRC),
    .AluSrcA(ALUSRCA), .MemToReg(MM2REG), .RegDst(REGDST), .IrWrite(IRW), .PcWrite(PCW), .RegWrite(REGW),
    .MemWrite(MMW), .MemRead(MMR), .Beq(BEQ), .Bne(BNE), .Func(FUNC), .ALU_OP(ALUOP));
  Multiplexer #(.select(1), .width(5), .disabled("Z"), .enable("false")) multiplexer_4 (
    .in0(IR[20:16]), .in1(IR[15:11]), .out(multiplexer_4_out), .sel(\多周期硬布线控制器_1_regdst ));
  Shifter #(.width(32), .shift("ll")) shifter_1 (
    .in({multiplexer_2_out, IR[15:0]}), .\dist (5'b00010), .out(shifter_1_out));
  // RegisterFile registerfile_1: pin names not known; wires that end beside it: CLK, multiplexer_4_out, IR[25:21], IR[20:16], registerfile_1_p5, registerfile_1_p6, registerfile_1_p7
  Register #(.width(32), .trigger("rising"), .Select("low")) A (
    .D(registerfile_1_p5), .Q(registerfile_1_p7), .clk(CLK), .clr(RST));  // open: en
  Register #(.width(32), .trigger("rising"), .Select("low")) B (
    .D(registerfile_1_p6), .Q(MDin), .clk(CLK), .clr(RST));  // open: en
  Multiplexer #(.select(1), .width(32), .disabled("Z"), .enable("false")) multiplexer_5 (
    .in0(PC), .in1(registerfile_1_p7), .out(multiplexer_5_out), .sel(\多周期硬布线控制器_1_alusrca ));
  Multiplexer #(.select(2), .width(32), .disabled("Z"), .enable("false")) multiplexer_6 (
    .in0(MDin), .in1(32'h4), .in2({multiplexer_2_out, IR[15:0]}), .in3(shifter_1_out),
    .out(multiplexer_6_out), .sel(\多周期硬布线控制器_1_alusrcb ));
  // Probe on multiplexer_5_out
  MIPS_ALU mips_alu_1 (
    .X(multiplexer_5_out), .Y(multiplexer_6_out), .AluOP(\多周期硬布线控制器_1_alu_op ), .Equal(mips_alu_1_equal),
    .Result(mips_alu_1_result));  // open: Result_2
  // Probe on multiplexer_6_out
  not not_2 (not_2_out, mips_alu_1_equal);
  // Probe on mips_alu_1_result
  and and_1 (and_1_out, \多周期硬布线控制器_1_beq , mips_alu_1_equal);
  and and_2 (and_2_out, \多周期硬布线控制器_1_bne , not_2_out);
  or or_1 (or_1_out, \多周期硬布线控制器_1_pcwrite , and_1_out, and_2_out);
  Register #(.width(32), .trigger("rising"), .Select("low")) C (
    .D(mips_alu_1_result), .Q(C_q), .clk(CLK), .clr(RST));  // open: en
  // Probe on C_q
  Multiplexer #(.select(1), .width(32), .disabled("Z"), .enable("false")) multiplexer_7 (
    .in0(mips_alu_1_result), .in1(C_q), .out(multiplexer_7_out), .sel(\多周期硬布线控制器_1_pcsrc ));

  // Notes on the sheet:
  //   控制位
  //   加载sort.hex，程序执行会停机并进行内存排序
  //   暂停节拍，不能为0
  //   用这个时钟源需要去掉电路中的其他时钟源
  //   戳工具置1进入计数暂停模式，ctrl+k时钟自动运行到对应节拍暂停
  //   ctrl+k关闭时钟连续运行，将控制位置零，进入单步调试模式调试
  //   参考值：891
  //   可计数暂停的时钟源
  //   部件
  //   选择器
  //   为方便自动评测，需要输出PC，IR，寄存器文件写入端口RDin，内存写入端口MDin等信号，以上引脚不能悬空
  //   部件
  //   选择器
  //   指令译码
endmodule

// 硬布线控制器
module \多周期硬布线控制器  (
  input  [5:0] OP,
  input  [5:0] Func,
  input  CLK,
  input  RST,
  output [3:0] ALU_OP,
  output Bne,
  output Beq,
  output MemRead,
  output MemWrite,
  output RegWrite,
  output PcWrite,
  output IrWrite,
  output RegDst,
  output MemToReg,
  output [3:0] \当前状态 ,
  output [1:0] AluSrcB,
  output AluSrcA,
  output PCsrc,
  output IorD
);

  wire ADD, ADDI, BEQ_t, BNE_t, comparator_6_eq, LW, P, R_TYPE, SLT, SW, SysCall;
  wire [1:0] ALU_Control;
  wire [3:0] multiplexer_1_out, multiplexer_2_out, or_1_out, rom_1_data, \状态机fsm_1_n0 ;

  Comparator #(.width(6), .mode("twosComplement")) comparator_1 (.a(OP), .b(6'b100011), .eq(LW));  // open: gt, lt
  Comparator #(.width(6), .mode("twosComplement")) comparator_2 (.a(OP), .b(6'b101011), .eq(SW));  // open: gt, lt
  Comparator #(.width(6), .mode("twosComplement")) comparator_3 (.a(OP), .b(6'b000100), .eq(BEQ_t));  // open: gt, lt
  Comparator #(.width(6), .mode("twosComplement")) comparator_4 (.a(OP), .b(6'b000101), .eq(BNE_t));  // open: gt, lt
  Comparator #(.width(6), .mode("twosComplement")) comparator_5 (.a(OP), .b(6'b001000), .eq(ADDI));  // open: gt, lt
  Comparator #(.width(6), .mode("twosComplement")) comparator_6 (
    .a(OP), .b({6{1'b0}}), .eq(comparator_6_eq));  // open: gt, lt
  and and_1 (R_TYPE, ~SysCall, comparator_6_eq);  // AND_Gate
  \状态机FSM  \u_状态机fsm_1  (
    .S3(\当前状态 [3]), .S2(\当前状态 [2]), .S1(\当前状态 [1]), .S0(\当前状态 [0]), .R_Type(R_TYPE), .ADDI(ADDI), .LW(LW),
    .N3(\状态机fsm_1_n0 [3]), .SW(SW), .BEQ(BEQ_t), .BNE(BNE_t), .SYSCALL(SysCall), .N2(\状态机fsm_1_n0 [2]),
    .N1(\状态机fsm_1_n0 [1]), .N0(\状态机fsm_1_n0 [0]));
  Comparator #(.width(6), .mode("twosComplement")) comparator_7 (.a(Func), .b(6'b100000), .eq(ADD));  // open: gt, lt
  Comparator #(.width(6), .mode("twosComplement")) comparator_8 (.a(Func), .b(6'b101010), .eq(SLT));  // open: gt, lt
  and and_2 (SysCall, ~SLT, ~ADD, comparator_6_eq);  // AND_Gate
  Register #(.width(4), .trigger("rising"), .Select("low")) register_1 (
    .D(\状态机fsm_1_n0 ), .Q(\当前状态 ), .clk(CLK), .clr(RST));  // open: en
  // Probe on \当前状态 
  \硬布线微指令  \u_硬布线微指令_1  (.in_1(\当前状态 ));  // open: out_2
  ROM #(.addrWidth(4), .dataWidth(21), .Select("high")) rom_1 (
    .addr(\当前状态 ),
    .data({IorD, PCsrc, AluSrcA, AluSrcB, MemToReg, RegDst, IrWrite, PcWrite, RegWrite, MemWrite, MemRead, Beq, Bne, ALU_Control, P, rom_1_data}));
  Multiplexer #(.select(1), .width(4), .disabled("Z"), .enable("false")) multiplexer_1 (
    .in0(4'b0000), .in1(4'b0101), .out(multiplexer_1_out), .sel(ADD));
  Multiplexer #(.select(1), .width(4), .disabled("Z"), .enable("false")) multiplexer_2 (
    .in0(4'b0000), .in1(4'b1011), .out(multiplexer_2_out), .sel(SLT));
  assign or_1_out = 4'b0000 | multiplexer_1_out | multiplexer_2_out;  // OR_Gate or_1, 4 bits wide
  Multiplexer #(.select(2), .width(4), .disabled("Z"), .enable("false")) multiplexer_3 (
    .in0(4'b0101), .in1(4'b0110), .in3(or_1_out), .out(ALU_OP), .sel(ALU_Control));  // open: in2

  // Notes on the sheet:
  //   指令译码信号
  //   现态
  //   组合逻辑
  //   指令译码逻辑
  //   次态
  //   给出简单的逻辑实现对应指令译码信号，LW、SW、BEQ、BNE、ADDI、ADD、SLT、SYSCALL、R_TYPE。
  //   状态寄存器
  //   contents of rom_1 (hex, n*v repeats v):
  //   13201 30010 60003 100204 8800 60006 100400 40048 4800 c0100 c0080 6000c 800 10004d
  //   ALU控制器逻辑
  //   根据ALU_Control的值决定运算器运算选择控制信号ALU_OP的值
  //   注意R_TYPE表示R型运算指令，SYSCALL是特殊的R型指令，不属于这个类别
  //   ALU_Control= 00 运算器做加法
  //   ALU_Control= 01 运算器做减法
  //   ALU_Control= 10 运算方式由Func决定 
endmodule

// 控制器状态机
module \状态机FSM  (
  input  S3,
  input  S2,
  input  S1,
  input  S0,
  input  R_Type,
  input  ADDI,
  input  LW,
  input  SW,
  input  BEQ,
  input  BNE,
  input  SYSCALL,
  output N3,
  output N2,
  output N1,
  output N0
);

  wire and_1_out, and_2_out, and_3_out, and_4_out, and_5_out, and_6_out, and_7_out, and_8_out, and_9_out,
       and_10_out, and_11_out, and_12_out, and_13_out, and_14_out, and_15_out, and_16_out, and_17_out,
       and_18_out, and_19_out, and_20_out, and_21_out, and_22_out, and_23_out, and_24_out, and_25_out,
       and_26_out, and_27_out, and_28_out, not_1_out, not_2_out, not_3_out, not_4_out, not_5_out, not_6_out,
       not_7_out, not_8_out, not_9_out, not_10_out, not_11_out, not_12_out, not_13_out, not_14_out,
       not_15_out, not_16_out, not_17_out, not_18_out, not_19_out, not_20_out, not_21_out, not_22_out,
       not_23_out, not_24_out, not_25_out, not_26_out, not_27_out, not_28_out, not_29_out, not_30_out,
       not_31_out, not_32_out, not_33_out, not_34_out, not_35_out, not_36_out, not_37_out, not_38_out,
       not_39_out, not_40_out, not_41_out, not_42_out, not_43_out, not_44_out, not_45_out, not_46_out,
       not_47_out, not_48_out, not_49_out, not_50_out, not_51_out, not_52_out, not_53_out, not_54_out,
       not_55_out, not_56_out, not_57_out, not_58_out, not_59_out, not_60_out, not_61_out, not_62_out,
       not_63_out, not_64_out, not_65_out, not_66_out, not_67_out, not_68_out, not_69_out, not_70_out;

  not not_1 (not_1_out, S3);
  not not_2 (not_2_out, S3);
  not not_3 (not_3_out, S2);
  not not_4 (not_4_out, S1);
  not not_5 (not_5_out, S3);
  not not_6 (not_6_out, S2);
  not not_7 (not_7_out, S1);
  not not_8 (not_8_out, S3);
  not not_9 (not_9_out, S2);
  not not_10 (not_10_out, S1);
  not not_11 (not_11_out, S2);
  not not_12 (not_12_out, S3);
  not not_13 (not_13_out, S2);
  not not_14 (not_14_out, S1);
  not not_15 (not_15_out, S1);
  not not_16 (not_16_out, S3);
  not not_17 (not_17_out, S2);
  not not_18 (not_18_out, S3);
  not not_19 (not_19_out, S2);
  not not_20 (not_20_out, S1);
  not not_21 (not_21_out, S3);
  not not_22 (not_22_out, S1);
  not not_23 (not_23_out, S3);
  not not_24 (not_24_out, S2);
  not not_25 (not_25_out, S1);
  not not_26 (not_26_out, S2);
  not not_27 (not_27_out, S3);
  not not_28 (not_28_out, S2);
  not not_29 (not_29_out, S1);
  not not_30 (not_30_out, S1);
  not not_31 (not_31_out, S3);
  not not_32 (not_32_out, S2);
  not not_33 (not_33_out, S1);
  not not_34 (not_34_out, S3);
  not not_35 (not_35_out, S2);
  not not_36 (not_36_out, S0);
  not not_37 (not_37_out, S3);
  not not_38 (not_38_out, S1);
  not not_39 (not_39_out, S3);
  not not_40 (not_40_out, S2);
  not not_41 (not_41_out, S1);
  not not_42 (not_42_out, S3);
  not not_43 (not_43_out, S2);
  not not_44 (not_44_out, S1);
  not not_45 (not_45_out, S3);
  not not_46 (not_46_out, S2);
  not not_47 (not_47_out, S1);
  not not_48 (not_48_out, S3);
  not not_49 (not_49_out, S2);
  not not_50 (not_50_out, S1);
  not not_51 (not_51_out, S0);
  not not_52 (not_52_out, S3);
  not not_53 (not_53_out, S2);
  not not_54 (not_54_out, S0);
  not not_55 (not_55_out, S3);
  not not_56 (not_56_out, S2);
  not not_57 (not_57_out, S1);
  not not_58 (not_58_out, S3);
  not not_59 (not_59_out, S2);
  not not_60 (not_60_out, S1);
  not not_61 (not_61_out, S3);
  not not_62 (not_62_out, S2);
  not not_63 (not_63_out, S1);
  not not_64 (not_64_out, S3);
  not not_65 (not_65_out, S2);
  not not_66 (not_66_out, S1);
  not not_67 (not_67_out, S3);
  not not_68 (not_68_out, S2);
  not not_69 (not_69_out, S1);
  not not_70 (not_70_out, S1);
  and and_1 (and_1_out, not_1_out, S2, S1, S0);
  and and_2 (and_2_out, not_2_out, not_3_out, not_4_out, S0, BEQ);
  and and_3 (and_3_out, not_5_out, not_6_out, not_7_out, S0, BNE);
  and and_4 (and_4_out, not_8_out, not_9_out, not_10_out, S0, ADDI);
  and and_5 (and_5_out, S3, not_11_out, S1, S0);
  and and_6 (and_6_out, not_12_out, not_13_out, not_14_out, S0, SYSCALL);
  and and_7 (and_7_out, S3, S2, not_15_out, S0);
  and and_8 (and_8_out, not_16_out, not_17_out, S1, S0);
  and and_9 (and_9_out, not_18_out, not_19_out, not_20_out, S0, SW);
  and and_10 (and_10_out, not_21_out, S2, not_22_out, S0);
  and and_11 (and_11_out, not_23_out, not_24_out, not_25_out, S0, R_Type);
  and and_12 (and_12_out, S3, not_26_out, S1, S0);
  and and_13 (and_13_out, not_27_out, not_28_out, not_29_out, S0, SYSCALL);
  and and_14 (and_14_out, S3, S2, not_30_out, S0);
  and and_15 (and_15_out, not_31_out, not_32_out, not_33_out, S0, LW);
  and and_16 (and_16_out, not_34_out, not_35_out, S1, not_36_out);
  and and_17 (and_17_out, not_37_out, S2, not_38_out, S0);
  and and_18 (and_18_out, not_39_out, not_40_out, not_41_out, S0, R_Type);
  and and_19 (and_19_out, not_42_out, not_43_out, not_44_out, S0, BNE);
  and and_20 (and_20_out, not_45_out, not_46_out, not_47_out, S0, ADDI);
  and and_21 (and_21_out, not_48_out, not_49_out, not_50_out, not_51_out);
  and and_22 (and_22_out, not_52_out, not_53_out, S1, not_54_out);
  and and_23 (and_23_out, not_55_out, not_56_out, not_57_out, S0, SW);
  and and_24 (and_24_out, not_58_out, not_59_out, not_60_out, S0, R_Type);
  and and_25 (and_25_out, not_61_out, not_62_out, not_63_out, S0, BEQ);
  and and_26 (and_26_out, not_64_out, not_65_out, not_66_out, S0, ADDI);
  and and_27 (and_27_out, not_67_out, not_68_out, not_69_out, S0, SYSCALL);
  and and_28 (and_28_out, S3, S2, not_70_out, S0);
  or or_1 (N3, and_1_out, and_2_out, and_3_out, and_4_out, and_5_out, and_6_out, and_7_out);
  or or_2 (N2, and_8_out, and_9_out, and_10_out, and_11_out, and_12_out, and_13_out, and_14_out);
  or or_3 (N1, and_15_out, and_16_out, and_17_out, and_18_out, and_19_out, and_20_out);
  or or_4 (N0, and_21_out, and_22_out, and_23_out, and_24_out, and_25_out, and_26_out, and_27_out, and_28_out);
endmodule

module MIPS_Regifile (
  input  [31:0] Din,
  input  Clk,
  input  WE,
  input  [4:0] R1_num,
  input  [4:0] R2_num,
  input  [4:0] W_num,
  output [31:0] R1,
  output [31:0] R2
);

  // RegisterFile registerfile_1: pin names not known; wires that end beside it: Din, Clk, WE, W_num, R1_num, R2_num, R1, R2
endmodule

// ALU
module MIPS_ALU (
  input  [31:0] X,
  input  [31:0] Y,
  input  [3:0] AluOP,
  output Equal,
  output [31:0] Result,
  output [31:0] Result_2
);

  wire [0:0] comparator_1_lt, comparator_2_lt;
  wire [31:0] adder_1_out, AND_out, divider_1_out, divider_1_rem, multiplier_1_cout, multiplier_1_out,
       NOR_out, OR_out, shifter_1_out, shifter_2_out, shifter_3_out, subtractor_1_out, XOR_out;

  assign AND_out = X & Y;  // AND_Gate AND, 32 bits wide
  assign OR_out = X | Y;  // OR_Gate OR, 32 bits wide
  Shifter #(.width(32), .shift("ll")) shifter_1 (.in(X), .\dist (Y[4:0]), .out(shifter_1_out));
  Shifter #(.width(32), .shift("ar")) shifter_2 (.in(X), .\dist (Y[4:0]), .out(shifter_2_out));
  Shifter #(.width(32), .shift("lr")) shifter_3 (.in(X), .\dist (Y[4:0]), .out(shifter_3_out));
  Multiplier #(.width(32)) multiplier_1 (.a(X), .b(Y), .out(multiplier_1_out), .cout(multiplier_1_cout));  // open: cin
  Divider #(.width(32)) divider_1 (.a(X), .b(Y), .out(divider_1_out), .rem(divider_1_rem));  // open: upper
  Adder #(.width(32)) adder_1 (.a(X), .b(Y), .out(adder_1_out));  // open: cin, cout
  Subtractor #(.width(32)) subtractor_1 (.a(X), .b(Y), .out(subtractor_1_out));  // open: bin, bout
  assign XOR_out = X ^ Y;  // XOR_Gate XOR, 32 bits wide
  assign NOR_out = ~(X | Y);  // NOR_Gate NOR, 32 bits wide
  Comparator #(.width(32), .mode("twosComplement")) comparator_1 (
    .a(X), .b(Y), .eq(Equal), .lt(comparator_1_lt[0]));  // open: gt
  Comparator #(.width(32), .mode("unsigned")) comparator_2 (.a(X), .b(Y), .lt(comparator_2_lt[0]));  // open: gt, eq
  Multiplexer #(.select(4), .width(32), .disabled("Z"), .enable("false")) multiplexer_1 (
    .in0(shifter_1_out), .in1(shifter_2_out), .in2(shifter_3_out), .in3(multiplier_1_out),
    .in4(divider_1_out), .in5(adder_1_out), .in6(subtractor_1_out), .in7(AND_out), .in8(OR_out),
    .in9(XOR_out), .in10(NOR_out), .in11({{31{1'b0}}, comparator_1_lt[0]}),
    .in12({{31{1'b0}}, comparator_2_lt[0]}), .in13({32{1'b0}}), .in14({32{1'b0}}), .in15({32{1'b0}}),
    .out(Result), .sel(AluOP));
  Multiplexer #(.select(4), .width(32), .disabled("Z"), .enable("false")) multiplexer_2 (
    .in0({32{1'b0}}), .in1({32{1'b0}}), .in2({32{1'b0}}), .in3(multiplier_1_cout), .in4(divider_1_rem),
    .in5({32{1'b0}}), .in6({32{1'b0}}), .in7({32{1'b0}}), .in8({32{1'b0}}), .in9({32{1'b0}}),
    .in10({32{1'b0}}), .in11({32{1'b0}}), .in12({32{1'b0}}), .in13({32{1'b0}}), .in14({32{1'b0}}),
    .in15({32{1'b0}}), .out(Result_2), .sel(AluOP));

  // Other names for the same wires on the sheet: Result2[31:0] = Result_2; S[3:0] = AluOP

  // Notes on the sheet:
  //   不要改变此引脚区域内容，也不要改变ALU封装形式
  //   输入引脚
  //   输出引脚
endmodule

module \微程序控制器  (
  input  a,
  input  b,
  input  c,
  input  d,
  output x,
  output y,
  output z,
  output u,
  output v,
  output w,
  output s,
  output t,
  output x2,
  output x3,
  output x4,
  output x5,
  output x6,
  output x7,
  output x8,
  output x9,
  output x10,
  output x11,
  output x12,
  output x13,
  output x14
);

  wire and_1_out, and_2_out, and_3_out, and_4_out, and_5_out, and_6_out, and_7_out, and_8_out, and_9_out,
       and_10_out, and_11_out, and_12_out, and_15_out, and_16_out, and_18_out, and_19_out, and_20_out,
       and_21_out, and_22_out, and_25_out, and_26_out, and_31_out, and_32_out, and_33_out, and_34_out,
       and_35_out, and_36_out, and_37_out, and_38_out, not_1_out, not_2_out, not_3_out, not_4_out, not_5_out,
       not_6_out, not_7_out, not_8_out, not_9_out, not_10_out, not_11_out, not_12_out, not_13_out,
       not_14_out, not_15_out, not_16_out, not_17_out, not_18_out, not_19_out, not_20_out, not_21_out,
       not_22_out, not_23_out, not_24_out, not_25_out, not_26_out, not_27_out, not_28_out, not_29_out,
       not_30_out, not_31_out, not_32_out, not_33_out, not_34_out, not_35_out, not_36_out, not_37_out,
       not_38_out, not_39_out, not_40_out, not_41_out, not_42_out, not_43_out, not_44_out, not_45_out,
       not_46_out, not_47_out, not_48_out, not_49_out, not_50_out, not_51_out, not_52_out, not_53_out,
       not_54_out, not_55_out, not_56_out, not_57_out, not_58_out, not_59_out, not_60_out, not_61_out;

  not not_1 (not_1_out, a);
  and and_1 (and_1_out, not_1_out, not_2_out, not_3_out);
  not not_2 (not_2_out, b);
  not not_3 (not_3_out, d);
  and and_2 (and_2_out, a, b, d);
  not not_4 (not_4_out, a);
  not not_5 (not_5_out, b);
  not not_6 (not_6_out, d);
  not not_7 (not_7_out, a);
  not not_8 (not_8_out, c);
  not not_9 (not_9_out, b);
  and and_3 (and_3_out, not_9_out, c, d);
  and and_4 (and_4_out, b, not_10_out, d);
  not not_10 (not_10_out, c);
  and and_5 (and_5_out, b, c, d);
  and and_6 (and_6_out, a, c, d);
  and and_7 (and_7_out, a, b, d);
  not not_11 (not_11_out, a);
  not not_12 (not_12_out, b);
  not not_13 (not_13_out, c);
  and and_8 (and_8_out, b, c, d);
  and and_9 (and_9_out, a, b, d);
  and and_10 (and_10_out, b, c, d);
  not not_14 (not_14_out, c);
  and and_11 (and_11_out, a, not_14_out, d);
  and and_12 (and_12_out, a, c, not_15_out);
  not not_15 (not_15_out, d);
  and and_13 (t, a, c, not_16_out);
  not not_16 (not_16_out, d);
  not not_17 (not_17_out, b);
  not not_18 (not_18_out, c);
  not not_19 (not_19_out, a);
  not not_20 (not_20_out, b);
  not not_21 (not_21_out, c);
  not not_22 (not_22_out, d);
  not not_23 (not_23_out, a);
  not not_24 (not_24_out, b);
  and and_14 (x4, b, c, not_25_out);
  not not_25 (not_25_out, d);
  and and_15 (and_15_out, b, not_26_out, not_27_out);
  not not_26 (not_26_out, c);
  not not_27 (not_27_out, d);
  and and_16 (and_16_out, a, not_28_out, not_29_out);
  not not_28 (not_28_out, c);
  not not_29 (not_29_out, d);
  not not_30 (not_30_out, a);
  not not_31 (not_31_out, b);
  not not_32 (not_32_out, c);
  not not_33 (not_33_out, d);
  not not_34 (not_34_out, a);
  not not_35 (not_35_out, b);
  not not_36 (not_36_out, c);
  not not_37 (not_37_out, d);
  not not_38 (not_38_out, b);
  not not_39 (not_39_out, c);
  not not_40 (not_40_out, d);
  not not_41 (not_41_out, a);
  not not_42 (not_42_out, c);
  not not_43 (not_43_out, d);
  not not_44 (not_44_out, a);
  not not_45 (not_45_out, b);
  and and_17 (x10, not_44_out, not_45_out, not_46_out);
  not not_46 (not_46_out, c);
  not not_47 (not_47_out, a);
  not not_48 (not_48_out, c);
  not not_49 (not_49_out, a);
  not not_50 (not_50_out, b);
  not not_51 (not_51_out, d);
  not not_52 (not_52_out, b);
  and and_18 (and_18_out, not_52_out, c, not_53_out);
  not not_53 (not_53_out, d);
  not not_54 (not_54_out, a);
  and and_19 (and_19_out, not_54_out, b, d);
  not not_55 (not_55_out, b);
  and and_20 (and_20_out, a, not_55_out, d);
  not not_56 (not_56_out, b);
  not not_57 (not_57_out, c);
  not not_58 (not_58_out, d);
  not not_59 (not_59_out, a);
  not not_60 (not_60_out, b);
  not not_61 (not_61_out, d);
  or or_1 (x, and_1_out, and_2_out);
  and and_21 (and_21_out, not_4_out, not_5_out, c, not_6_out);
  or or_2 (y, and_21_out, and_22_out);
  and and_22 (and_22_out, not_7_out, b, not_8_out, d);
  or or_3 (z, and_3_out, and_4_out);
  or or_4 (u, and_5_out, and_6_out, and_7_out);
  and and_23 (v, not_11_out, not_12_out, not_13_out, d);
  or or_5 (w, and_8_out, and_9_out);
  or or_6 (s, and_10_out, and_11_out, and_12_out);
  and and_24 (x2, a, not_17_out, not_18_out, d);
  and and_25 (and_25_out, not_19_out, not_20_out, not_21_out, not_22_out);
  or or_7 (x3, and_25_out, and_26_out);
  and and_26 (and_26_out, not_23_out, not_24_out, c, d);
  or or_8 (x5, and_15_out, and_16_out);
  and and_27 (x6, not_30_out, not_31_out, not_32_out, not_33_out);
  and and_28 (x7, not_34_out, not_35_out, not_36_out, not_37_out);
  and and_29 (x8, a, not_38_out, not_39_out, not_40_out);
  and and_30 (x9, not_41_out, b, not_42_out, not_43_out);
  and and_31 (and_31_out, not_47_out, not_48_out, d);
  or or_9 (x11, and_31_out, and_32_out, and_33_out);
  and and_32 (and_32_out, not_49_out, not_50_out, c, not_51_out);
  and and_33 (and_33_out, a, c, d);
  or or_10 (x12, and_18_out, and_19_out, and_20_out);
  and and_34 (and_34_out, a, not_56_out, not_57_out, d);
  or or_11 (x13, and_34_out, and_35_out);
  and and_35 (and_35_out, a, c, not_58_out);
  and and_36 (and_36_out, not_59_out, not_60_out, c, d);
  and and_37 (and_37_out, b, c, not_61_out);
  or or_12 (x14, and_36_out, and_37_out, and_38_out);
  and and_38 (and_38_out, a, b, d);
endmodule

module \硬布线微指令  (
  input  [3:0] in_1,
  output [20:0] out_2
);

  // Probe on in_1
  \微程序控制器  \u_微程序控制器_1  (
    .a(in_1[3]), .b(in_1[2]), .c(in_1[1]), .d(in_1[0]), .x(out_2[0]), .y(out_2[1]), .z(out_2[2]),
    .u(out_2[3]), .v(out_2[4]), .w(out_2[5]), .s(out_2[6]), .t(out_2[7]), .x2(out_2[8]), .x3(out_2[9]),
    .x4(out_2[10]), .x5(out_2[11]), .x6(out_2[12]), .x7(out_2[13]), .x8(out_2[14]), .x9(out_2[15]),
    .x10(out_2[16]), .x11(out_2[17]), .x12(out_2[18]), .x13(out_2[19]), .x14(out_2[20]));
  // Probe on out_2
endmodule
