// Logisim project 数据通路重构加载反汇编库.circ as structural Verilog: 12 circuits, main circuit ◇多周期MIPS(微程序)
module \单周期MIPS_硬布线  (
  output RegWrite,
  output MemWrite,
  output [31:0] PC,
  output [31:0] IR,
  output [31:0] RDin,
  output [31:0] MDin
);

  wire CLK, RST;
  wire [15:0] \总周期数 ;

  Button \u_总复位  (.out(RST));
  Clock #(.highDuration(1), .lowDuration(1)) clock_1 (.out(CLK));
  // Probe on \总周期数 
  // Probe on \总周期数 

  // Notes on the sheet:
  //   程序运行结束后可停机，查看数据存储器中80单元的排序情况是有符号降序
  //   总周期数参考值：224
  //   为方便自动评测，需要输出PC，IR，寄存器文件写入端口RDin，内存写入端口MDin等信号
endmodule

// 单周期硬布线控制器
module \单周期硬布线控制器  (
  input  [5:0] OP,
  input  [5:0] Func,
  output [3:0] ALU_OP,
  output RegDst,
  output RegWrite,
  output MemToReg,
  output MemWrite,
  output AluSrc,
  output Beq,
  output Bne,
  output Halt
);

  wire ADDI, BEQ_t, BNE_t, comparator_6_eq, LW, SW;
  wire [5:0] undriven, undriven_2, undriven_3, undriven_4, undriven_5;

  Comparator #(.width(6), .mode("twosComplement")) comparator_1 (.a(OP), .b(undriven), .eq(LW));  // open: gt, lt
  Comparator #(.width(6), .mode("twosComplement")) comparator_2 (.a(OP), .b(undriven_2), .eq(SW));  // open: gt, lt
  Comparator #(.width(6), .mode("twosComplement")) comparator_3 (.a(OP), .b(undriven_3), .eq(BEQ_t));  // open: gt, lt
  Comparator #(.width(6), .mode("twosComplement")) comparator_4 (.a(OP), .b(undriven_4), .eq(BNE_t));  // open: gt, lt
  Comparator #(.width(6), .mode("twosComplement")) comparator_5 (.a(OP), .b(undriven_5), .eq(ADDI));  // open: gt, lt
  Comparator #(.width(6), .mode("twosComplement")) comparator_6 (
    .a(OP), .b({6{1'b0}}), .eq(comparator_6_eq));  // open: gt, lt

  // Notes on the sheet:
  //   指令译码信号
  //   指令译码逻辑
  //   给出简单的逻辑实现对应指令译码信号，LW、SW、BEQ、BNE、ADDI、ADD、SLT、SYSCALL、R_TYPE。
  //   ALU控制器逻辑
  //   注意R_TYPE表示R型运算指令，SYSCALL是特殊的R型指令，不属于这个类别
  //   根据指令译码信号实现控制器输出控制信号的逻辑
  //   给出简单的逻辑实现ALU_OP与OP、Func之间的对应关系
  //   控制信号
endmodule

module \多周期MIPS_微程序  (
  output RegWrite,
  output MemWrite,
  output [31:0] PC,
  output [31:0] IR,
  output [31:0] RDin,
  output [31:0] MDin
);

  wire ALUAS, ALUEQ, and_1_out, and_2_out, BEQ, BNE, CLK, comparator_1_eq, ID, IRW, M2R, MR, not_1_out, PCEN,
       PCS, PCW, REGDST, RST;
  wire [1:0] ALUBS;
  wire [3:0] ALUOP, S;
  wire [4:0] multiplexer_3_out;
  wire [15:0] \总周期数 ;
  wire [31:0] A_q, C, DR, IMM16EX, mips_alu_1_result, mips_probe_1_p2, multiplexer_1_out, multiplexer_4_out,
       multiplexer_5_out, PCNEX, registerfile_1_p7, registerfile_1_p8, shifter_1_out;

  Button \u_总复位  (.out(RST));
  Clock #(.highDuration(1), .lowDuration(1)) clock_1 (.out(CLK));
  Multiplexer #(.select(1), .width(32), .disabled("Z"), .enable("false")) multiplexer_1 (
    .in0(PC), .in1(C), .out(multiplexer_1_out), .sel(ID));
  // Probe on S
  Register #(.width(32), .trigger("rising"), .Select("low")) u_PC (.D(PCNEX), .en(PCEN), .Q(PC), .clk(CLK), .clr(RST));
  // Probe on \总周期数 
  // Probe on \总周期数 
  // Mips_Probe mips_probe_1: pin names not known; wires that end beside it: RST, mips_probe_1_p2
  RAM #(.addrWidth(24), .dataWidth(32), .bus("separate"), .Select("high")) ram_1 (
    .addr(multiplexer_1_out[25:2]), .din(MDin), .data(mips_probe_1_p2), .str(MemWrite), .clk(CLK));  // open: sel, ld, clr
  assign IMM16EX = {{16{IR[15]}}, IR[15:0]};  // Bit_Extender bit_extender_1
  and and_1 (and_1_out, BEQ, ALUEQ);
  and and_2 (and_2_out, ~ALUEQ, BNE);  // AND_Gate
  // Mips_Probe mips_probe_2: pin names not known; wires that end beside it: IR
  Register #(.width(32), .trigger("rising"), .Select("low")) u_IR (
    .D(mips_probe_1_p2), .en(IRW), .Q(IR), .clk(CLK), .clr(RST));
  Register #(.width(32), .trigger("rising"), .Select("low")) u_DR (
    .D(mips_probe_1_p2), .Q(DR), .clk(CLK), .clr(RST));  // open: en
  Shifter #(.width(32), .shift("ll")) shifter_1 (.in(IMM16EX), .\dist (5'b00010), .out(shifter_1_out));
  or or_1 (PCEN, and_1_out, and_2_out, PCW);
  Multiplexer #(.select(1), .width(32), .disabled("Z"), .enable("false")) multiplexer_2 (
    .in0(C), .in1(DR), .out(RDin), .sel(M2R));
  Comparator #(.width(4), .mode("twosComplement")) comparator_1 (
    .a(S), .b(4'b1101), .eq(comparator_1_eq));  // open: gt, lt
  Multiplexer #(.select(1), .width(5), .disabled("Z"), .enable("false")) multiplexer_3 (
    .in0(IR[20:16]), .in1(IR[15:11]), .out(multiplexer_3_out), .sel(REGDST));
  not not_1 (not_1_out, comparator_1_eq);
  // RegisterFile registerfile_1: pin names not known; wires that end beside it: RDin, CLK, RegWrite, multiplexer_3_out, IR[25:21], IR[20:16], registerfile_1_p7, registerfile_1_p8
  Counter #(.width(16), .max('hffff), .ongoal("wrap"), .trigger("rising"), .behavior("old")) counter_1 (
    .count(not_1_out), .Q(\总周期数 ), .clk(CLK), .clr(RST));  // open: load, D, carry, preset
  Register #(.width(32), .trigger("rising"), .Select("low")) A (
    .D(registerfile_1_p7), .Q(A_q), .clk(CLK), .clr(RST));  // open: en
  Register #(.width(32), .trigger("rising"), .Select("low")) B (
    .D(registerfile_1_p8), .Q(MDin), .clk(CLK), .clr(RST));  // open: en
  Multiplexer #(.select(1), .width(32), .disabled("Z"), .enable("false")) multiplexer_4 (
    .in0(PC), .in1(A_q), .out(multiplexer_4_out), .sel(ALUAS));
  Multiplexer #(.select(2), .width(32), .disabled("Z"), .enable("false")) multiplexer_5 (
    .in0(MDin), .in1(32'h4), .in2(IMM16EX), .in3(shifter_1_out), .out(multiplexer_5_out), .sel(ALUBS));
  MIPS_ALU mips_alu_1 (
    .X(multiplexer_4_out), .Y(multiplexer_5_out), .AluOP(ALUOP), .Equal(ALUEQ), .Result(mips_alu_1_result));  // open: Result_2
  \多周期微程序控制器  \u_多周期微程序控制器_1  (
    .PcWrite(PCW), .Beq(BEQ), .PCsrc(PCS), .AluSrcB(ALUBS), .AluSrcA(ALUAS), .RegWrite(RegWrite),
    .MemToReg(M2R), .RegDst(REGDST), .IorD(ID), .MemWrite(MemWrite), .MemRead(MR), .IrWrite(IRW), .Bne(BNE),
    .CLK(CLK), .\当前微指令地址 (S), .RST(RST), .OP(IR[31:26]), .ALU_OP(ALUOP), .Func(IR[5:0]));
  Register #(.width(32), .trigger("rising"), .Select("low")) u_C (
    .D(mips_alu_1_result), .Q(C), .clk(CLK), .clr(RST));  // open: en
  Multiplexer #(.select(1), .width(32), .disabled("Z"), .enable("false")) multiplexer_6 (
    .in0(mips_alu_1_result), .in1(C), .out(PCNEX), .sel(PCS));

  // Other names for the same wires on the sheet: ADD26[25:0] = IR[25:0]; FUNC[5:0] = IR[5:0]; IMM16[15:0] = IR[15:0];
  //   SHAMT[4:0] = IR[10:6]; R3[4:0] = IR[15:11]; R2[4:0] = IR[20:16]; R1[4:0] = IR[25:21]; OP[5:0] = IR[31:26];
  //   MW = MemWrite; RW = RegWrite; 微地址[3:0] = S

  // Notes on the sheet:
  //   加载sort.hex，程序执行会停机并进行内存排序
  //   参考值：891
  //   为方便自动评测，需要输出PC，IR，寄存器文件写入端口RDin，内存写入端口MDin等信号
endmodule

// 微程序控制器
module \多周期微程序控制器  (
  input  [5:0] OP,
  input  [5:0] Func,
  input  CLK,
  input  RST,
  output [3:0] ALU_OP,
  output Bne,
  output Beq,
  output MemRead,
  output MemWrite,
  output RegWrite,
  output PcWrite,
  output IrWrite,
  output RegDst,
  output MemToReg,
  output [3:0] \当前微指令地址 ,
  output [1:0] AluSrcB,
  output AluSrcA,
  output PCsrc,
  output IorD
);

  wire ADD, ADDI, BEQ_t, BNE_t, comparator_6_eq, LW, P, R_TYPE, SLT, SW, SysCall;
  wire [1:0] ALU_Control;
  wire [3:0] multiplexer_1_out, multiplexer_2_out, multiplexer_3_out, or_1_out, rom_1_data, \微程序地址转移逻辑_1_s0 ;

  Comparator #(.width(6), .mode("twosComplement")) comparator_1 (.a(OP), .b(6'b100011), .eq(LW));  // open: gt, lt
  Comparator #(.width(6), .mode("twosComplement")) comparator_2 (.a(OP), .b(6'b101011), .eq(SW));  // open: gt, lt
  Comparator #(.width(6), .mode("twosComplement")) comparator_3 (.a(OP), .b(6'b000100), .eq(BEQ_t));  // open: gt, lt
  Comparator #(.width(6), .mode("twosComplement")) comparator_4 (.a(OP), .b(6'b000101), .eq(BNE_t));  // open: gt, lt
  Comparator #(.width(6), .mode("twosComplement")) comparator_5 (.a(OP), .b(6'b001000), .eq(ADDI));  // open: gt, lt
  Comparator #(.width(6), .mode("twosComplement")) comparator_6 (
    .a(OP), .b({6{1'b0}}), .eq(comparator_6_eq));  // open: gt, lt
  and and_1 (R_TYPE, ~SysCall, comparator_6_eq);  // AND_Gate
  \微程序地址转移逻辑  \u_微程序地址转移逻辑_1  (
    .R_Type(R_TYPE), .S3(\微程序地址转移逻辑_1_s0 [3]), .ADDI(ADDI), .S2(\微程序地址转移逻辑_1_s0 [2]), .LW(LW),
    .S1(\微程序地址转移逻辑_1_s0 [1]), .SW(SW), .S0(\微程序地址转移逻辑_1_s0 [0]), .BEQ(BEQ_t), .BNE(BNE_t), .SYSCALL(SysCall));
  Comparator #(.width(6), .mode("twosComplement")) comparator_7 (.a(Func), .b(6'b100000), .eq(ADD));  // open: gt, lt
  Comparator #(.width(6), .mode("twosComplement")) comparator_8 (.a(Func), .b(6'b101010), .eq(SLT));  // open: gt, lt
  and and_2 (SysCall, ~SLT, ~ADD, comparator_6_eq);  // AND_Gate
  Register #(.width(4), .trigger("rising"), .Select("low")) register_1 (
    .D(multiplexer_1_out), .Q(\当前微指令地址 ), .clk(CLK), .clr(RST));  // open: en
  Multiplexer #(.select(1), .width(4), .disabled("Z"), .enable("false")) multiplexer_1 (
    .in0(rom_1_data), .in1(\微程序地址转移逻辑_1_s0 ), .out(multiplexer_1_out), .sel(P));
  ROM #(.addrWidth(4), .dataWidth(21), .Select("high")) rom_1 (
    .addr(\当前微指令地址 ),
    .data({IorD, PCsrc, AluSrcA, AluSrcB, MemToReg, RegDst, IrWrite, PcWrite, RegWrite, MemWrite, MemRead, Beq, Bne, ALU_Control, P, rom_1_data}));
  Multiplexer #(.select(1), .width(4), .disabled("Z"), .enable("false")) multiplexer_2 (
    .in0(4'b0000), .in1(4'b0101), .out(multiplexer_2_out), .sel(ADD));
  Multiplexer #(.select(1), .width(4), .disabled("Z"), .enable("false")) multiplexer_3 (
    .in0(4'b0000), .in1(4'b1011), .out(multiplexer_3_out), .sel(SLT));
  assign or_1_out = 4'b0000 | multiplexer_2_out | multiplexer_3_out;  // OR_Gate or_1, 4 bits wide
  Multiplexer #(.select(2), .width(4), .disabled("Z"), .enable("false")) multiplexer_4 (
    .in0(4'b0101), .in1(4'b0110), .in2(or_1_out), .out(ALU_OP), .sel(ALU_Control));  // open: in3

  // Notes on the sheet:
  //   指令译码信号
  //   根据指令进行微程序地址转移
  //   指令译码逻辑
  //   给出简单的逻辑实现对应指令译码信号，LW、SW、BEQ、BNE、ADDI、ADD、SLT、SYSCALL、R_TYPE。
  //   下址字段
  //   微程序
  //   入口地址
  //   判断逻辑
  //   μAR
  //   控制存储器
  //   contents of rom_1 (hex, n*v repeats v):
  //   13201 30010 60003 100204 8800 60006 100400 40048 4800 c0100 c0080 6000c 800 10004d
  //   微命令
  //   ALU控制器逻辑
  //   根据ALU_Control的值决定运算器运算选择控制信号ALU_OP的值
  //   注意R_TYPE表示R型运算指令，SYSCALL是特殊的R型指令，不属于这个类别
  //   微指令
  //   下址字段
  //   判断逻辑
  //   ALU_Control= 00 运算器做加法
  //   ALU_Control= 01 运算器做减法
  //   ALU_Control= 10 运算方式由Func决定 
endmodule

// 地址转移逻辑
module \微程序地址转移逻辑  (
  input  R_Type,
  input  ADDI,
  input  LW,
  input  SW,
  input  BEQ,
  input  BNE,
  input  SYSCALL,
  output S3,
  output S2,
  output S1,
  output S0
);

  wire [3:0] multiplexer_1_out, multiplexer_2_out, multiplexer_3_out, multiplexer_4_out, multiplexer_5_out,
       multiplexer_6_out, multiplexer_7_out;

  Multiplexer #(.select(1), .width(4), .disabled("Z"), .enable("false")) multiplexer_1 (
    .in0(4'b0000), .in1(4'b0111), .out(multiplexer_1_out), .sel(R_Type));
  Multiplexer #(.select(1), .width(4), .disabled("Z"), .enable("false")) multiplexer_2 (
    .in0(4'b0000), .in1(4'b1011), .out(multiplexer_2_out), .sel(ADDI));
  Multiplexer #(.select(1), .width(4), .disabled("Z"), .enable("false")) multiplexer_3 (
    .in0(4'b0000), .in1(4'b0010), .out(multiplexer_3_out), .sel(LW));
  Multiplexer #(.select(1), .width(4), .disabled("Z"), .enable("false")) multiplexer_4 (
    .in0(4'b0000), .in1(4'b0101), .out(multiplexer_4_out), .sel(SW));
  Multiplexer #(.select(1), .width(4), .disabled("Z"), .enable("false")) multiplexer_5 (
    .in0(4'b0000), .in1(4'b1001), .out(multiplexer_5_out), .sel(BEQ));
  Multiplexer #(.select(1), .width(4), .disabled("Z"), .enable("false")) multiplexer_6 (
    .in0(4'b0000), .in1(4'b1010), .out(multiplexer_6_out), .sel(BNE));
  Multiplexer #(.select(1), .width(4), .disabled("Z"), .enable("false")) multiplexer_7 (
    .in0(4'b0000), .in1(4'b1101), .out(multiplexer_7_out), .sel(SYSCALL));
  assign {S3, S2, S1, S0} = multiplexer_1_out | multiplexer_2_out | multiplexer_3_out | multiplexer_4_out | multiplexer_5_out | multiplexer_6_out | multiplexer_7_out;  // OR_Gate or_1, 4 bits wide
endmodule

module \多周期MIPS_硬布线  (
  output RegWrite,
  output MemWrite,
  output [31:0] PC,
  output [31:0] IR,
  output [31:0] RDin,
  output [31:0] MDin
);

  wire ALUAS, ALUEQ, and_1_out, and_2_out, BEQ, BNE, CLK, comparator_1_eq, ID, IRW, M2R, MR, not_1_out, PCEN,
       PCS, PCW, REGDST, RST;
  wire [1:0] ALUBS;
  wire [3:0] ALUOP, S;
  wire [4:0] multiplexer_3_out;
  wire [15:0] \总周期数 ;
  wire [31:0] A_q, C, DR, IMM16EX, mips_alu_1_result, mips_probe_1_p2, multiplexer_1_out, multiplexer_4_out,
       multiplexer_5_out, PCNEX, registerfile_1_p7, registerfile_1_p8, shifter_1_out;

  Button \u_总复位  (.out(RST));
  Clock #(.highDuration(1), .lowDuration(1)) clock_1 (.out(CLK));
  Multiplexer #(.select(1), .width(32), .disabled("Z"), .enable("false")) multiplexer_1 (
    .in0(PC), .in1(C), .out(multiplexer_1_out), .sel(ID));
  // Probe on S
  Register #(.width(32), .trigger("rising"), .Select("low")) u_PC (.D(PCNEX), .en(PCEN), .Q(PC), .clk(CLK), .clr(RST));
  // Probe on \总周期数 
  // Probe on \总周期数 
  // Mips_Probe mips_probe_1: pin names not known; wires that end beside it: RST, mips_probe_1_p2
  RAM #(.addrWidth(24), .dataWidth(32), .bus("separate"), .Select("high")) ram_1 (
    .addr(multiplexer_1_out[25:2]), .din(MDin), .data(mips_probe_1_p2), .str(MemWrite), .clk(CLK));  // open: sel, ld, clr
  assign IMM16EX = {{16{IR[15]}}, IR[15:0]};  // Bit_Extender bit_extender_1
  and and_1 (and_1_out, BEQ, ALUEQ);
  and and_2 (and_2_out, ~ALUEQ, BNE);  // AND_Gate
  // Mips_Probe mips_probe_2: pin names not known; wires that end beside it: IR
  Register #(.width(32), .trigger("rising"), .Select("low")) u_IR (
    .D(mips_probe_1_p2), .en(IRW), .Q(IR), .clk(CLK), .clr(RST));
  Register #(.width(32), .trigger("rising"), .Select("low")) u_DR (
    .D(mips_probe_1_p2), .Q(DR), .clk(CLK), .clr(RST));  // open: en
  Shifter #(.width(32), .shift("ll")) shifter_1 (.in(IMM16EX), .\dist (5'b00010), .out(shifter_1_out));
  or or_1 (PCEN, and_1_out, and_2_out, PCW);
  Multiplexer #(.select(1), .width(32), .disabled("Z"), .enable("false")) multiplexer_2 (
    .in0(C), .in1(DR), .out(RDin), .sel(M2R));
  Comparator #(.width(4), .mode("twosComplement")) comparator_1 (
    .a(S), .b(4'b1101), .eq(comparator_1_eq));  // open: gt, lt
  // Probe on S
  Multiplexer #(.select(1), .width(5), .disabled("Z"), .enable("false")) multiplexer_3 (
    .in0(IR[20:16]), .in1(IR[15:11]), .out(multiplexer_3_out), .sel(REGDST));
  not not_1 (not_1_out, comparator_1_eq);
  // RegisterFile registerfile_1: pin names not known; wires that end beside it: RDin, CLK, RegWrite, multiplexer_3_out, IR[25:21], IR[20:16], registerfile_1_p7, registerfile_1_p8
  Counter #(.width(16), .max('hffff), .ongoal("wrap"), .trigger("rising"), .behavior("old")) counter_1 (
    .count(not_1_out), .Q(\总周期数 ), .clk(CLK), .clr(RST));  // open: load, D, carry, preset
  Register #(.width(32), .trigger("rising"), .Select("low")) A (
    .D(registerfile_1_p7), .Q(A_q), .clk(CLK), .clr(RST));  // open: en
  Register #(.width(32), .trigger("rising"), .Select("low")) B (
    .D(registerfile_1_p8), .Q(MDin), .clk(CLK), .clr(RST));  // open: en
  Multiplexer #(.select(1), .width(32), .disabled("Z"), .enable("false")) multiplexer_4 (
    .in0(PC), .in1(A_q), .out(multiplexer_4_out), .sel(ALUAS));
  Multiplexer #(.select(2), .width(32), .disabled("Z"), .enable("false")) multiplexer_5 (
    .in0(MDin), .in1(32'h4), .in2(IMM16EX), .in3(shifter_1_out), .out(multiplexer_5_out), .sel(ALUBS));
  MIPS_ALU mips_alu_1 (
    .X(multiplexer_4_out), .Y(multiplexer_5_out), .AluOP(ALUOP), .Equal(ALUEQ), .Result(mips_alu_1_result));  // open: Result_2
  \多周期硬布线控制器  \u_多周期硬布线控制器_1  (
    .RST(RST), .AluSrcB(ALUBS), .OP(IR[31:26]), .CLK(CLK), .\当前状态 (S), .IorD(ID), .PCsrc(PCS),
    .AluSrcA(ALUAS), .MemToReg(M2R), .RegDst(REGDST), .IrWrite(IRW), .PcWrite(PCW), .RegWrite(RegWrite),
    .MemWrite(MemWrite), .MemRead(MR), .Beq(BEQ), .Bne(BNE), .Func(IR[5:0]), .ALU_OP(ALUOP));
  Register #(.width(32), .trigger("rising"), .Select("low")) u_C (
    .D(mips_alu_1_result), .Q(C), .clk(CLK), .clr(RST));  // open: en
  Multiplexer #(.select(1), .width(32), .disabled("Z"), .enable("false")) multiplexer_6 (
    .in0(mips_alu_1_result), .in1(C), .out(PCNEX), .sel(PCS));

  // Other names for the same wires on the sheet: ADD26[25:0] = IR[25:0]; FUNC[5:0] = IR[5:0]; IMM16[15:0] = IR[15:0];
  //   SHAMT[4:0] = IR[10:6]; R3[4:0] = IR[15:11]; R2[4:0] = IR[20:16]; R1[4:0] = IR[25:21]; OP[5:0] = IR[31:26];
  //   MW = MemWrite; RW = RegWrite; 微地址[3:0] = S; 现态[3:0] = S

  // Notes on the sheet:
  //   加载sort.hex，程序执行会停机并进行内存排序
  //   参考值：891
  //   为方便自动评测，需要输出PC，IR，寄存器文件写入端口RDin，内存写入端口MDin等信号
endmodule

// 硬布线控制器
module \多周期硬布线控制器  (
  input  [5:0] OP,
  input  [5:0] Func,
  input  CLK,
  input  RST,
  output [3:0] ALU_OP,
  output Bne,
  output Beq,
  output MemRead,
  output MemWrite,
  output RegWrite,
  output PcWrite,
  output IrWrite,
  output RegDst,
  output MemToReg,
  output [3:0] \当前状态 ,
  output [1:0] AluSrcB,
  output AluSrcA,
  output PCsrc,
  output IorD
);

  wire ADD, ADDI, BEQ_t, BNE_t, comparator_6_eq, LW, P, R_TYPE, SLT, SW, SysCall;
  wire [1:0] ALU_Control;
  wire [3:0] multiplexer_1_out, multiplexer_2_out, or_1_out, \状态机fsm_1_n0 , \硬布线微指令_1_out_2 ;

  Comparator #(.width(6), .mode("twosComplement")) comparator_1 (.a(OP), .b(6'b100011), .eq(LW));  // open: gt, lt
  Comparator #(.width(6), .mode("twosComplement")) comparator_2 (.a(OP), .b(6'b101011), .eq(SW));  // open: gt, lt
  Comparator #(.width(6), .mode("twosComplement")) comparator_3 (.a(OP), .b(6'b000100), .eq(BEQ_t));  // open: gt, lt
  Comparator #(.width(6), .mode("twosComplement")) comparator_4 (.a(OP), .b(6'b000101), .eq(BNE_t));  // open: gt, lt
  Comparator #(.width(6), .mode("twosComplement")) comparator_5 (.a(OP), .b(6'b001000), .eq(ADDI));  // open: gt, lt
  Comparator #(.width(6), .mode("twosComplement")) comparator_6 (
    .a(OP), .b({6{1'b0}}), .eq(comparator_6_eq));  // open: gt, lt
  and and_1 (R_TYPE, ~SysCall, comparator_6_eq);  // AND_Gate
  \状态机FSM  \u_状态机fsm_1  (
    .S3(\当前状态 [3]), .S2(\当前状态 [2]), .S1(\当前状态 [1]), .S0(\当前状态 [0]), .R_Type(R_TYPE), .ADDI(ADDI), .LW(LW),
    .N3(\状态机fsm_1_n0 [3]), .SW(SW), .BEQ(BEQ_t), .BNE(BNE_t), .SYSCALL(SysCall), .N2(\状态机fsm_1_n0 [2]),
    .N1(\状态机fsm_1_n0 [1]), .N0(\状态机fsm_1_n0 [0]));
  Comparator #(.width(6), .mode("twosComplement")) comparator_7 (.a(Func), .b(6'b100000), .eq(ADD));  // open: gt, lt
  Comparator #(.width(6), .mode("twosComplement")) comparator_8 (.a(Func), .b(6'b101010), .eq(SLT));  // open: gt, lt
  and and_2 (SysCall, ~SLT, ~ADD, comparator_6_eq);  // AND_Gate
  Register #(.width(4), .trigger("rising"), .Select("low")) register_1 (
    .D(\状态机fsm_1_n0 ), .Q(\当前状态 ), .clk(CLK), .clr(RST));  // open: en
  // Probe on \当前状态 
  \硬布线微指令  \u_硬布线微指令_1  (
    .in_1(\当前状态 ),
    .out_2({IorD, PCsrc, AluSrcA, AluSrcB, MemToReg, RegDst, IrWrite, PcWrite, RegWrite, MemWrite, MemRead, Beq, Bne, ALU_Control, P, \硬布线微指令_1_out_2 }));
  ROM #(.addrWidth(4), .dataWidth(21), .Select("high")) rom_1 (.addr(\当前状态 ));  // open: data
  Multiplexer #(.select(1), .width(4), .disabled("Z"), .enable("false")) multiplexer_1 (
    .in0(4'b0000), .in1(4'b0101), .out(multiplexer_1_out), .sel(ADD));
  Multiplexer #(.select(1), .width(4), .disabled("Z"), .enable("false")) multiplexer_2 (
    .in0(4'b0000), .in1(4'b1011), .out(multiplexer_2_out), .sel(SLT));
  assign or_1_out = 4'b0000 | multiplexer_1_out | multiplexer_2_out;  // OR_Gate or_1, 4 bits wide
  Multiplexer #(.select(2), .width(4), .disabled("Z"), .enable("false")) multiplexer_3 (
    .in0(4'b0101), .in1(4'b0110), .in2(or_1_out), .out(ALU_OP), .sel(ALU_Control));  // open: in3

  // Notes on the sheet:
  //   指令译码信号
  //   现态
  //   组合逻辑
  //   指令译码逻辑
  //   次态
  //   给出简单的逻辑实现对应指令译码信号，LW、SW、BEQ、BNE、ADDI、ADD、SLT、SYSCALL、R_TYPE。
  //   状态寄存器
  //   contents of rom_1 (hex, n*v repeats v):
  //   13201 30010 60003 100204 8800 60006 100400 40048 4800 c0100 c0080 6000c 800 10004d
  //   ALU控制器逻辑
  //   根据ALU_Control的值决定运算器运算选择控制信号ALU_OP的值
  //   注意R_TYPE表示R型运算指令，SYSCALL是特殊的R型指令，不属于这个类别
  //   ALU_Control= 00 运算器做加法
  //   ALU_Control= 01 运算器做减法
  //   ALU_Control= 10 运算方式由Func决定 
endmodule

// 控制器状态机
module \状态机FSM  (
  input  S3,
  input  S2,
  input  S1,
  input  S0,
  input  R_Type,
  input  ADDI,
  input  LW,
  input  SW,
  input  BEQ,
  input  BNE,
  input  SYSCALL,
  output N3,
  output N2,
  output N1,
  output N0
);

  wire and_1_out, and_2_out, and_3_out, and_4_out, and_5_out, and_6_out, and_7_out, and_8_out, and_9_out,
       and_10_out, and_11_out, and_12_out, and_13_out, and_14_out, and_15_out, and_16_out, and_17_out,
       and_18_out, and_19_out, and_20_out, and_21_out, and_22_out, and_23_out, and_24_out, and_25_out,
       and_26_out, and_27_out, and_28_out, not_1_out, not_2_out, not_3_out, not_4_out, not_5_out, not_6_out,
       not_7_out, not_8_out, not_9_out, not_10_out, not_11_out, not_12_out, not_13_out, not_14_out,
       not_15_out, not_16_out, not_17_out, not_18_out, not_19_out, not_20_out, not_21_out, not_22_out,
       not_23_out, not_24_out, not_25_out, not_26_out, not_27_out, not_28_out, not_29_out, not_30_out,
       not_31_out, not_32_out, not_33_out, not_34_out, not_35_out, not_36_out, not_37_out, not_38_out,
       not_39_out, not_40_out, not_41_out, not_42_out, not_43_out, not_44_out, not_45_out, not_46_out,
       not_47_out, not_48_out, not_49_out, not_50_out, not_51_out, not_52_out, not_53_out, not_54_out,
       not_55_out, not_56_out, not_57_out, not_58_out, not_59_out, not_60_out, not_61_out, not_62_out,
       not_63_out, not_64_out, not_65_out, not_66_out, not_67_out, not_68_out, not_69_out, not_70_out;

  not not_1 (not_1_out, S3);
  not not_2 (not_2_out, S3);
  not not_3 (not_3_out, S2);
  not not_4 (not_4_out, S1);
  not not_5 (not_5_out, S3);
  not not_6 (not_6_out, S2);
  not not_7 (not_7_out, S1);
  not not_8 (not_8_out, S3);
  not not_9 (not_9_out, S2);
  not not_10 (not_10_out, S1);
  not not_11 (not_11_out, S2);
  not not_12 (not_12_out, S3);
  not not_13 (not_13_out, S2);
  not not_14 (not_14_out, S1);
  not not_15 (not_15_out, S1);
  not not_16 (not_16_out, S3);
  not not_17 (not_17_out, S2);
  not not_18 (not_18_out, S3);
  not not_19 (not_19_out, S2);
  not not_20 (not_20_out, S1);
  not not_21 (not_21_out, S3);
  not not_22 (not_22_out, S1);
  not not_23 (not_23_out, S3);
  not not_24 (not_24_out, S2);
  not not_25 (not_25_out, S1);
  not not_26 (not_26_out, S2);
  not not_27 (not_27_out, S3);
  not not_28 (not_28_out, S2);
  not not_29 (not_29_out, S1);
  not not_30 (not_30_out, S1);
  not not_31 (not_31_out, S3);
  not not_32 (not_32_out, S2);
  not not_33 (not_33_out, S1);
  not not_34 (not_34_out, S3);
  not not_35 (not_35_out, S2);
  not not_36 (not_36_out, S0);
  not not_37 (not_37_out, S3);
  not not_38 (not_38_out, S1);
  not not_39 (not_39_out, S3);
  not not_40 (not_40_out, S2);
  not not_41 (not_41_out, S1);
  not not_42 (not_42_out, S3);
  not not_43 (not_43_out, S2);
  not not_44 (not_44_out, S1);
  not not_45 (not_45_out, S3);
  not not_46 (not_46_out, S2);
  not not_47 (not_47_out, S1);
  not not_48 (not_48_out, S3);
  not not_49 (not_49_out, S2);
  not not_50 (not_50_out, S1);
  not not_51 (not_51_out, S0);
  not not_52 (not_52_out, S3);
  not not_53 (not_53_out, S2);
  not not_54 (not_54_out, S0);
  not not_55 (not_55_out, S3);
  not not_56 (not_56_out, S2);
  not not_57 (not_57_out, S1);
  not not_58 (not_58_out, S3);
  not not_59 (not_59_out, S2);
  not not_60 (not_60_out, S1);
  not not_61 (not_61_out, S3);
  not not_62 (not_62_out, S2);
  not not_63 (not_63_out, S1);
  not not_64 (not_64_out, S3);
  not not_65 (not_65_out, S2);
  not not_66 (not_66_out, S1);
  not not_67 (not_67_out, S3);
  not not_68 (not_68_out, S2);
  not not_69 (not_69_out, S1);
  not not_70 (not_70_out, S1);
  and and_1 (and_1_out, not_1_out, S2, S1, S0);
  and and_2 (and_2_out, not_2_out, not_3_out, not_4_out, S0, BEQ);
  and and_3 (and_3_out, not_5_out, not_6_out, not_7_out, S0, BNE);
  and and_4 (and_4_out, not_8_out, not_9_out, not_10_out, S0, ADDI);
  and and_5 (and_5_out, S3, not_11_out, S1, S0);
  and and_6 (and_6_out, not_12_out, not_13_out, not_14_out, S0, SYSCALL);
  and and_7 (and_7_out, S3, S2, not_15_out, S0);
  and and_8 (and_8_out, not_16_out, not_17_out, S1, S0);
  and and_9 (and_9_out, not_18_out, not_19_out, not_20_out, S0, SW);
  and and_10 (and_10_out, not_21_out, S2, not_22_out, S0);
  and and_11 (and_11_out, not_23_out, not_24_out, not_25_out, S0, R_Type);
  and and_12 (and_12_out, S3, not_26_out, S1, S0);
  and and_13 (and_13_out, not_27_out, not_28_out, not_29_out, S0, SYSCALL);
  and and_14 (and_14_out, S3, S2, not_30_out, S0);
  and and_15 (and_15_out, not_31_out, not_32_out, not_33_out, S0, LW);
  and and_16 (and_16_out, not_34_out, not_35_out, S1, not_36_out);
  and and_17 (and_17_out, not_37_out, S2, not_38_out, S0);
  and and_18 (and_18_out, not_39_out, not_40_out, not_41_out, S0, R_Type);
  and and_19 (and_19_out, not_42_out, not_43_out, not_44_out, S0, BNE);
  and and_20 (and_20_out, not_45_out, not_46_out, not_47_out, S0, ADDI);
  and and_21 (and_21_out, not_48_out, not_49_out, not_50_out, not_51_out);
  and and_22 (and_22_out, not_52_out, not_53_out, S1, not_54_out);
  and and_23 (and_23_out, not_55_out, not_56_out, not_57_out, S0, SW);
  and and_24 (and_24_out, not_58_out, not_59_out, not_60_out, S0, R_Type);
  and and_25 (and_25_out, not_61_out, not_62_out, not_63_out, S0, BEQ);
  and and_26 (and_26_out, not_64_out, not_65_out, not_66_out, S0, ADDI);
  and and_27 (and_27_out, not_67_out, not_68_out, not_69_out, S0, SYSCALL);
  and and_28 (and_28_out, S3, S2, not_70_out, S0);
  or or_1 (N3, and_1_out, and_2_out, and_3_out, and_4_out, and_5_out, and_6_out, and_7_out);
  or or_2 (N2, and_8_out, and_9_out, and_10_out, and_11_out, and_12_out, and_13_out, and_14_out);
  or or_3 (N1, and_15_out, and_16_out, and_17_out, and_18_out, and_19_out, and_20_out);
  or or_4 (N0, and_21_out, and_22_out, and_23_out, and_24_out, and_25_out, and_26_out, and_27_out, and_28_out);
endmodule

module MIPS_Regifile (
  input  [31:0] Din,
  input  Clk,
  input  WE,
  input  [4:0] R1_num,
  input  [4:0] W_num,
  input  [4:0] R2_num,
  output [31:0] R1,
  output [31:0] R2
);

  // RegisterFile registerfile_1: pin names not known; wires that end beside it: Din, Clk, WE, W_num, R1_num, R2_num, R1, R2
endmodule

module \微程序控制器  (
  input  a,
  input  b,
  input  c,
  input  d,
  output x,
  output y,
  output z,
  output u,
  output v,
  output w,
  output s,
  output t,
  output x2,
  output x3,
  output x4,
  output x5,
  output x6,
  output x7,
  output x8,
  output x9,
  output x10,
  output x11,
  output x12,
  output x13,
  output x14
);

  wire nand_1_out, nand_2_out, nand_3_out, nand_4_out, nand_5_out, nand_6_out, nand_7_out, nand_8_out,
       nand_9_out, nand_10_out, nand_11_out, nand_12_out, nand_13_out, nand_14_out, nand_15_out, nand_16_out,
       nand_17_out, nand_18_out, nand_19_out, nand_20_out, nand_21_out, nand_22_out, nand_23_out,
       nand_24_out, nand_25_out, nand_26_out, nand_27_out, nand_28_out, nand_29_out, nand_30_out,
       nand_31_out, nand_32_out, nand_33_out, nand_34_out, nand_35_out, nand_36_out, nand_37_out,
       nand_38_out, nand_39_out, nand_40_out, nand_41_out, nand_42_out, nand_43_out, nand_44_out,
       nand_45_out, nand_46_out, nand_47_out, nand_48_out, nand_49_out, nand_50_out, nand_51_out,
       nand_52_out, nand_53_out, nand_54_out, nand_55_out, nand_56_out, nand_57_out, nand_58_out,
       nand_59_out, nand_60_out, nand_61_out, nand_62_out, nand_63_out, nand_64_out, nand_65_out,
       nand_66_out, nand_67_out, nand_68_out, nand_69_out, nand_70_out, nand_71_out, nand_72_out,
       nand_73_out, nand_74_out, nand_75_out, nand_76_out, nand_77_out, nand_78_out, nand_79_out,
       nand_80_out, nand_81_out, nand_82_out, nand_83_out, nand_84_out, nand_85_out, nand_86_out,
       nand_87_out, nand_88_out, nand_89_out, nand_90_out, nand_91_out, nand_92_out, nand_93_out,
       nand_94_out, nand_95_out, nand_96_out, nand_97_out, nand_98_out, nand_99_out, nand_100_out,
       nand_101_out, nand_102_out, nand_103_out, nand_104_out, nand_105_out, nand_106_out, nand_107_out,
       nand_108_out, nand_109_out, nand_110_out, nand_111_out, nand_112_out, nand_113_out, nand_114_out,
       nand_115_out, nand_116_out, nand_117_out, nand_118_out, nand_119_out, nand_120_out, nand_121_out,
       nand_122_out, nand_123_out, nand_124_out, nand_125_out, nand_126_out, nand_127_out, nand_128_out,
       nand_129_out, nand_130_out, nand_131_out, nand_132_out, nand_133_out, nand_134_out, nand_135_out,
       nand_136_out, nand_137_out, nand_138_out, nand_139_out, nand_140_out, nand_141_out, nand_142_out,
       nand_143_out, nand_144_out, nand_145_out, nand_146_out, nand_147_out, nand_148_out, nand_149_out,
       nand_150_out, nand_151_out, nand_152_out, nand_153_out, nand_154_out, nand_155_out, nand_156_out,
       nand_157_out, nand_158_out, nand_159_out, nand_160_out, nand_161_out, nand_162_out, nand_163_out,
       nand_166_out, nand_167_out, nand_168_out, nand_170_out, nand_171_out, nand_172_out, nand_173_out,
       nand_174_out, nand_175_out, nand_176_out, nand_177_out, nand_178_out, nand_179_out, nand_180_out,
       nand_181_out, nand_182_out, nand_183_out, nand_184_out, nand_185_out, nand_186_out, nand_187_out,
       nand_191_out, nand_192_out, nand_202_out, nand_203_out, nand_204_out, nand_205_out, nand_207_out,
       nand_208_out, nand_210_out, nand_211_out, nand_212_out, nand_213_out, nand_214_out, nand_215_out;

  nand nand_1 (nand_1_out, a, a);
  nand nand_2 (nand_2_out, b, b);
  nand nand_3 (nand_3_out, a, a);
  nand nand_4 (nand_4_out, b, b);
  nand nand_5 (nand_5_out, d, d);
  nand nand_6 (nand_6_out, a, a);
  nand nand_7 (nand_7_out, c, c);
  nand nand_8 (nand_8_out, b, b);
  nand nand_9 (nand_9_out, c, c);
  nand nand_10 (nand_10_out, b, c);
  nand nand_11 (nand_11_out, a, c);
  nand nand_12 (nand_12_out, a, a);
  nand nand_13 (nand_13_out, b, b);
  nand nand_14 (nand_14_out, c, c);
  nand nand_15 (nand_15_out, b, c);
  nand nand_16 (nand_16_out, a, b);
  nand nand_17 (nand_17_out, a, c);
  nand nand_18 (nand_18_out, b, b);
  nand nand_19 (nand_19_out, c, c);
  nand nand_20 (nand_20_out, a, a);
  nand nand_21 (nand_21_out, b, b);
  nand nand_22 (nand_22_out, c, c);
  nand nand_23 (nand_23_out, d, d);
  nand nand_24 (nand_24_out, a, a);
  nand nand_25 (nand_25_out, b, b);
  nand nand_26 (nand_26_out, b, c);
  nand nand_27 (nand_27_out, c, c);
  nand nand_28 (nand_28_out, c, c);
  nand nand_29 (nand_29_out, a, a);
  nand nand_30 (nand_30_out, b, b);
  nand nand_31 (nand_31_out, c, c);
  nand nand_32 (nand_32_out, d, d);
  nand nand_33 (nand_33_out, a, a);
  nand nand_34 (nand_34_out, b, b);
  nand nand_35 (nand_35_out, c, c);
  nand nand_36 (nand_36_out, d, d);
  nand nand_37 (nand_37_out, b, b);
  nand nand_38 (nand_38_out, c, c);
  nand nand_39 (nand_39_out, d, d);
  nand nand_40 (nand_40_out, a, a);
  nand nand_41 (nand_41_out, c, c);
  nand nand_42 (nand_42_out, d, d);
  nand nand_43 (nand_43_out, a, a);
  nand nand_44 (nand_44_out, b, b);
  nand nand_45 (nand_45_out, a, a);
  nand nand_46 (nand_46_out, c, c);
  nand nand_47 (nand_47_out, a, a);
  nand nand_48 (nand_48_out, b, b);
  nand nand_49 (nand_49_out, d, d);
  nand nand_50 (nand_50_out, b, b);
  nand nand_51 (nand_51_out, a, a);
  nand nand_52 (nand_52_out, b, b);
  nand nand_53 (nand_53_out, c, c);
  nand nand_54 (nand_54_out, a, a);
  nand nand_55 (nand_55_out, b, b);
  nand nand_56 (nand_56_out, nand_1_out, nand_2_out);
  nand nand_57 (nand_57_out, a, b);
  nand nand_58 (nand_58_out, nand_3_out, nand_4_out);
  nand nand_59 (nand_59_out, c, nand_5_out);
  nand nand_60 (nand_60_out, nand_6_out, b);
  nand nand_61 (nand_61_out, nand_7_out, d);
  nand nand_62 (nand_62_out, nand_8_out, c);
  nand nand_63 (nand_63_out, b, nand_9_out);
  nand nand_64 (nand_64_out, nand_10_out, nand_10_out);
  nand nand_65 (nand_65_out, nand_11_out, nand_11_out);
  nand nand_66 (nand_66_out, nand_12_out, nand_13_out);
  nand nand_67 (nand_67_out, nand_14_out, d);
  nand nand_68 (nand_68_out, nand_15_out, nand_15_out);
  nand nand_69 (nand_69_out, nand_16_out, nand_16_out);
  nand nand_70 (nand_70_out, nand_17_out, nand_17_out);
  nand nand_71 (nand_71_out, d, d);
  nand nand_72 (nand_72_out, a, nand_18_out);
  nand nand_73 (nand_73_out, nand_19_out, d);
  nand nand_74 (nand_74_out, nand_20_out, nand_21_out);
  nand nand_75 (nand_75_out, nand_22_out, nand_23_out);
  nand nand_76 (nand_76_out, nand_24_out, nand_25_out);
  nand nand_77 (nand_77_out, c, d);
  nand nand_78 (nand_78_out, nand_26_out, nand_26_out);
  nand nand_79 (nand_79_out, d, d);
  nand nand_80 (nand_80_out, b, nand_27_out);
  nand nand_81 (nand_81_out, a, nand_28_out);
  nand nand_82 (nand_82_out, nand_29_out, nand_30_out);
  nand nand_83 (nand_83_out, nand_31_out, nand_32_out);
  nand nand_84 (nand_84_out, nand_33_out, nand_34_out);
  nand nand_85 (nand_85_out, nand_35_out, nand_36_out);
  nand nand_86 (nand_86_out, a, nand_37_out);
  nand nand_87 (nand_87_out, nand_38_out, nand_39_out);
  nand nand_88 (nand_88_out, nand_40_out, b);
  nand nand_89 (nand_89_out, nand_41_out, nand_42_out);
  nand nand_90 (nand_90_out, nand_43_out, nand_44_out);
  nand nand_91 (nand_91_out, nand_45_out, nand_46_out);
  nand nand_92 (nand_92_out, nand_47_out, nand_48_out);
  nand nand_93 (nand_93_out, c, nand_49_out);
  nand nand_94 (nand_94_out, nand_50_out, c);
  nand nand_95 (nand_95_out, nand_51_out, b);
  nand nand_96 (nand_96_out, a, nand_52_out);
  nand nand_97 (nand_97_out, nand_53_out, d);
  nand nand_98 (nand_98_out, a, c);
  nand nand_99 (nand_99_out, nand_54_out, nand_55_out);
  nand nand_100 (nand_100_out, c, d);
  nand nand_101 (nand_101_out, b, c);
  nand nand_102 (nand_102_out, nand_56_out, nand_56_out);
  nand nand_103 (nand_103_out, d, d);
  nand nand_104 (nand_104_out, nand_57_out, nand_57_out);
  nand nand_105 (nand_105_out, nand_58_out, nand_58_out);
  nand nand_106 (nand_106_out, nand_59_out, nand_59_out);
  nand nand_107 (nand_107_out, nand_60_out, nand_60_out);
  nand nand_108 (nand_108_out, nand_61_out, nand_61_out);
  nand nand_109 (nand_109_out, nand_62_out, nand_62_out);
  nand nand_110 (nand_110_out, nand_63_out, nand_63_out);
  nand nand_111 (nand_111_out, nand_64_out, d);
  nand nand_112 (nand_112_out, nand_65_out, d);
  nand nand_113 (nand_113_out, a, b);
  nand nand_114 (nand_114_out, nand_66_out, nand_66_out);
  nand nand_115 (nand_115_out, nand_67_out, nand_67_out);
  nand nand_116 (nand_116_out, nand_68_out, d);
  nand nand_117 (nand_117_out, nand_69_out, d);
  nand nand_118 (nand_118_out, nand_70_out, nand_71_out);
  nand nand_119 (nand_119_out, nand_72_out, nand_72_out);
  nand nand_120 (nand_120_out, nand_73_out, nand_73_out);
  nand nand_121 (nand_121_out, nand_74_out, nand_74_out);
  nand nand_122 (nand_122_out, nand_75_out, nand_75_out);
  nand nand_123 (nand_123_out, nand_76_out, nand_76_out);
  nand nand_124 (nand_124_out, nand_77_out, nand_77_out);
  nand nand_125 (nand_125_out, nand_78_out, nand_79_out);
  nand nand_126 (nand_126_out, nand_80_out, nand_80_out);
  nand nand_127 (nand_127_out, d, d);
  nand nand_128 (nand_128_out, nand_81_out, nand_81_out);
  nand nand_129 (nand_129_out, d, d);
  nand nand_130 (nand_130_out, nand_82_out, nand_82_out);
  nand nand_131 (nand_131_out, nand_83_out, nand_83_out);
  nand nand_132 (nand_132_out, nand_84_out, nand_84_out);
  nand nand_133 (nand_133_out, nand_85_out, nand_85_out);
  nand nand_134 (nand_134_out, nand_86_out, nand_86_out);
  nand nand_135 (nand_135_out, nand_87_out, nand_87_out);
  nand nand_136 (nand_136_out, nand_88_out, nand_88_out);
  nand nand_137 (nand_137_out, nand_89_out, nand_89_out);
  nand nand_138 (nand_138_out, nand_90_out, nand_90_out);
  nand nand_139 (nand_139_out, c, c);
  nand nand_140 (nand_140_out, nand_91_out, nand_91_out);
  nand nand_141 (nand_141_out, nand_92_out, nand_92_out);
  nand nand_142 (nand_142_out, nand_93_out, nand_93_out);
  nand nand_143 (nand_143_out, nand_94_out, nand_94_out);
  nand nand_144 (nand_144_out, d, d);
  nand nand_145 (nand_145_out, nand_95_out, nand_95_out);
  nand nand_146 (nand_146_out, b, b);
  nand nand_147 (nand_147_out, nand_96_out, nand_96_out);
  nand nand_148 (nand_148_out, nand_97_out, nand_97_out);
  nand nand_149 (nand_149_out, nand_98_out, nand_98_out);
  nand nand_150 (nand_150_out, d, d);
  nand nand_151 (nand_151_out, nand_99_out, nand_99_out);
  nand nand_152 (nand_152_out, nand_100_out, nand_100_out);
  nand nand_153 (nand_153_out, nand_101_out, nand_101_out);
  nand nand_154 (nand_154_out, d, d);
  nand nand_155 (nand_155_out, nand_102_out, nand_103_out);
  nand nand_156 (nand_156_out, nand_104_out, d);
  nand nand_157 (nand_157_out, nand_105_out, nand_106_out);
  nand nand_158 (nand_158_out, nand_107_out, nand_108_out);
  nand nand_159 (nand_159_out, nand_109_out, d);
  nand nand_160 (nand_160_out, nand_110_out, d);
  nand nand_161 (nand_161_out, nand_111_out, nand_112_out);
  nand nand_162 (nand_162_out, nand_113_out, nand_113_out);
  nand nand_163 (nand_163_out, nand_114_out, nand_115_out);
  nand nand_164 (s, nand_116_out, nand_117_out);
  nand nand_165 (t, nand_118_out, nand_118_out);
  nand nand_166 (nand_166_out, nand_119_out, nand_120_out);
  nand nand_167 (nand_167_out, nand_121_out, nand_122_out);
  nand nand_168 (nand_168_out, nand_123_out, nand_124_out);
  nand nand_169 (x4, nand_125_out, nand_125_out);
  nand nand_170 (nand_170_out, nand_126_out, nand_127_out);
  nand nand_171 (nand_171_out, nand_128_out, nand_129_out);
  nand nand_172 (nand_172_out, nand_130_out, nand_131_out);
  nand nand_173 (nand_173_out, nand_132_out, nand_133_out);
  nand nand_174 (nand_174_out, nand_134_out, nand_135_out);
  nand nand_175 (nand_175_out, nand_136_out, nand_137_out);
  nand nand_176 (nand_176_out, nand_138_out, nand_139_out);
  nand nand_177 (nand_177_out, nand_140_out, d);
  nand nand_178 (nand_178_out, nand_141_out, nand_142_out);
  nand nand_179 (nand_179_out, a, c);
  nand nand_180 (nand_180_out, nand_143_out, nand_144_out);
  nand nand_181 (nand_181_out, nand_145_out, d);
  nand nand_182 (nand_182_out, a, nand_146_out);
  nand nand_183 (nand_183_out, nand_147_out, nand_148_out);
  nand nand_184 (nand_184_out, nand_149_out, nand_150_out);
  nand nand_185 (nand_185_out, nand_151_out, nand_152_out);
  nand nand_186 (nand_186_out, nand_153_out, nand_154_out);
  nand nand_187 (nand_187_out, a, b);
  nand nand_188 (x, nand_155_out, nand_156_out);
  nand nand_189 (y, nand_157_out, nand_158_out);
  nand nand_190 (z, nand_159_out, nand_160_out);
  nand nand_191 (nand_191_out, nand_161_out, nand_161_out);
  nand nand_192 (nand_192_out, nand_162_out, d);
  nand nand_193 (v, nand_163_out, nand_163_out);
  nand nand_194 (x2, nand_166_out, nand_166_out);
  nand nand_195 (x3, nand_167_out, nand_168_out);
  nand nand_196 (x5, nand_170_out, nand_171_out);
  nand nand_197 (x6, nand_172_out, nand_172_out);
  nand nand_198 (x7, nand_173_out, nand_173_out);
  nand nand_199 (x8, nand_174_out, nand_174_out);
  nand nand_200 (x9, nand_175_out, nand_175_out);
  nand nand_201 (x10, nand_176_out, nand_176_out);
  nand nand_202 (nand_202_out, nand_177_out, nand_178_out);
  nand nand_203 (nand_203_out, nand_179_out, nand_179_out);
  nand nand_204 (nand_204_out, nand_180_out, nand_181_out);
  nand nand_205 (nand_205_out, nand_182_out, nand_182_out);
  nand nand_206 (x13, nand_183_out, nand_184_out);
  nand nand_207 (nand_207_out, nand_185_out, nand_186_out);
  nand nand_208 (nand_208_out, nand_187_out, nand_187_out);
  nand nand_209 (u, nand_191_out, nand_192_out);
  nand nand_210 (nand_210_out, nand_202_out, nand_202_out);
  nand nand_211 (nand_211_out, nand_203_out, d);
  nand nand_212 (nand_212_out, nand_204_out, nand_204_out);
  nand nand_213 (nand_213_out, nand_205_out, d);
  nand nand_214 (nand_214_out, nand_207_out, nand_207_out);
  nand nand_215 (nand_215_out, nand_208_out, d);
  nand nand_216 (x11, nand_210_out, nand_211_out);
  nand nand_217 (x12, nand_212_out, nand_213_out);
  nand nand_218 (x14, nand_214_out, nand_215_out);

  assign w = 1'b0;
endmodule

module \硬布线微指令  (
  input  [3:0] in_1,
  output [20:0] out_2
);

  // Probe on in_1
  \微程序控制器  \u_微程序控制器_1  (
    .a(in_1[3]), .b(in_1[2]), .c(in_1[1]), .d(in_1[0]), .x(out_2[0]), .y(out_2[1]), .z(out_2[2]),
    .u(out_2[3]), .v(out_2[4]), .w(out_2[5]), .s(out_2[6]), .t(out_2[7]), .x2(out_2[8]), .x3(out_2[9]),
    .x4(out_2[10]), .x5(out_2[11]), .x6(out_2[12]), .x7(out_2[13]), .x8(out_2[14]), .x9(out_2[15]),
    .x10(out_2[16]), .x11(out_2[17]), .x12(out_2[18]), .x13(out_2[19]), .x14(out_2[20]));
  // Probe on out_2
endmodule

// ALU
module MIPS_ALU (
  input  [31:0] X,
  input  [31:0] Y,
  input  [3:0] AluOP,
  output Equal,
  output [31:0] Result,
  output [31:0] Result_2
);

  wire [0:0] comparator_1_lt, comparator_2_lt;
  wire [31:0] adder_1_out, AND_out, divider_1_out, divider_1_rem, multiplier_1_cout, multiplier_1_out,
       NOR_out, OR_out, shifter_1_out, shifter_2_out, shifter_3_out, subtractor_1_out, XOR_out;

  assign AND_out = X & Y;  // AND_Gate AND, 32 bits wide
  assign OR_out = X | Y;  // OR_Gate OR, 32 bits wide
  Shifter #(.width(32), .shift("ll")) shifter_1 (.in(X), .\dist (Y[4:0]), .out(shifter_1_out));
  Shifter #(.width(32), .shift("ar")) shifter_2 (.in(X), .\dist (Y[4:0]), .out(shifter_2_out));
  Shifter #(.width(32), .shift("lr")) shifter_3 (.in(X), .\dist (Y[4:0]), .out(shifter_3_out));
  Multiplier #(.width(32)) multiplier_1 (.a(X), .b(Y), .out(multiplier_1_out), .cout(multiplier_1_cout));  // open: cin
  Divider #(.width(32)) divider_1 (.a(X), .b(Y), .out(divider_1_out), .rem(divider_1_rem));  // open: upper
  Adder #(.width(32)) adder_1 (.a(X), .b(Y), .out(adder_1_out));  // open: cin, cout
  Subtractor #(.width(32)) subtractor_1 (.a(X), .b(Y), .out(subtractor_1_out));  // open: bin, bout
  assign XOR_out = X ^ Y;  // XOR_Gate XOR, 32 bits wide
  assign NOR_out = ~(X | Y);  // NOR_Gate NOR, 32 bits wide
  Comparator #(.width(32), .mode("twosComplement")) comparator_1 (
    .a(X), .b(Y), .eq(Equal), .lt(comparator_1_lt[0]));  // open: gt
  Comparator #(.width(32), .mode("unsigned")) comparator_2 (.a(X), .b(Y), .lt(comparator_2_lt[0]));  // open: gt, eq
  Multiplexer #(.select(4), .width(32), .disabled("Z"), .enable("false")) multiplexer_1 (
    .in0(shifter_1_out), .in1(shifter_2_out), .in2(shifter_3_out), .in3(multiplier_1_out),
    .in4(divider_1_out), .in5(adder_1_out), .in6(subtractor_1_out), .in7(AND_out), .in8(OR_out),
    .in9(XOR_out), .in10(NOR_out), .in11({{31{1'b0}}, comparator_1_lt[0]}),
    .in12({{31{1'b0}}, comparator_2_lt[0]}), .in13({32{1'b0}}), .in14({32{1'b0}}), .in15({32{1'b0}}),
    .out(Result), .sel(AluOP));
  Multiplexer #(.select(4), .width(32), .disabled("Z"), .enable("false")) multiplexer_2 (
    .in0({32{1'b0}}), .in1({32{1'b0}}), .in2({32{1'b0}}), .in3(multiplier_1_cout), .in4(divider_1_rem),
    .in5({32{1'b0}}), .in6({32{1'b0}}), .in7({32{1'b0}}), .in8({32{1'b0}}), .in9({32{1'b0}}),
    .in10({32{1'b0}}), .in11({32{1'b0}}), .in12({32{1'b0}}), .in13({32{1'b0}}), .in14({32{1'b0}}),
    .in15({32{1'b0}}), .out(Result_2), .sel(AluOP));

  // Other names for the same wires on the sheet: Result2[31:0] = Result_2; S[3:0] = AluOP

  // Notes on the sheet:
  //   不要改变此引脚区域内容，也不要改变ALU封装形式
  //   输入引脚
  //   输出引脚
endmodule
